// Logisim project CPU.circ as structural Verilog
module AND (
  input  in_1,
  input  in_2,
  output out_3
);

  wire nand_1_out;

  nand nand_1 (nand_1_out, in_1, in_2);
  nand nand_2 (out_3, nand_1_out, nand_1_out);
endmodule

module _3AND (
  input  in_1,
  input  in_2,
  input  in_3,
  output out_4
);

  wire and_1_out_3;

  AND and_1 (.in_1(in_1), .in_2(in_2), .out_3(and_1_out_3));
  AND and_2 (.in_1(and_1_out_3), .in_2(in_3), .out_3(out_4));
endmodule

module AND16 (
  input  in_1,
  input  in_2,
  input  in_3,
  input  in_4,
  input  in_5,
  input  in_6,
  input  in_7,
  input  in_8,
  input  in_9,
  input  in_10,
  input  in_11,
  input  in_12,
  input  in_13,
  input  in_14,
  input  in_15,
  input  in_16,
  input  in_17,
  input  in_18,
  input  in_19,
  input  in_20,
  input  in_21,
  input  in_22,
  input  in_23,
  input  in_24,
  input  in_25,
  input  in_26,
  input  in_27,
  input  in_28,
  input  in_29,
  input  in_30,
  input  in_31,
  input  in_32,
  output out_33,
  output out_34,
  output out_35,
  output out_36,
  output out_37,
  output out_38,
  output out_39,
  output out_40,
  output out_41,
  output out_42,
  output out_43,
  output out_44,
  output out_45,
  output out_46,
  output out_47,
  output out_48
);

  AND and_1 (.in_1(in_1), .in_2(in_17), .out_3(out_33));
  AND and_2 (.in_1(in_2), .in_2(in_18), .out_3(out_34));
  AND and_3 (.in_1(in_3), .in_2(in_19), .out_3(out_35));
  AND and_4 (.in_1(in_4), .in_2(in_20), .out_3(out_36));
  AND and_5 (.in_1(in_5), .in_2(in_21), .out_3(out_37));
  AND and_6 (.in_1(in_6), .in_2(in_22), .out_3(out_38));
  AND and_7 (.in_1(in_7), .in_2(in_23), .out_3(out_39));
  AND and_8 (.in_1(in_8), .in_2(in_24), .out_3(out_40));
  AND and_9 (.in_1(in_9), .in_2(in_25), .out_3(out_41));
  AND and_10 (.in_1(in_10), .in_2(in_26), .out_3(out_42));
  AND and_11 (.in_1(in_11), .in_2(in_27), .out_3(out_43));
  AND and_12 (.in_1(in_12), .in_2(in_28), .out_3(out_44));
  AND and_13 (.in_1(in_13), .in_2(in_29), .out_3(out_45));
  AND and_14 (.in_1(in_14), .in_2(in_30), .out_3(out_46));
  AND and_15 (.in_1(in_15), .in_2(in_31), .out_3(out_47));
  AND and_16 (.in_1(in_16), .in_2(in_32), .out_3(out_48));
endmodule

module OR (
  input  in_1,
  input  in_2,
  output out_3
);

  wire nand_1_out, nand_2_out;

  nand nand_1 (nand_1_out, in_1, in_1);
  nand nand_2 (nand_2_out, in_2, in_2);
  nand nand_3 (out_3, nand_1_out, nand_2_out);
endmodule

module OR16 (
  input  in_1,
  input  in_2,
  input  in_3,
  input  in_4,
  input  in_5,
  input  in_6,
  input  in_7,
  input  in_8,
  input  in_9,
  input  in_10,
  input  in_11,
  input  in_12,
  input  in_13,
  input  in_14,
  input  in_15,
  input  in_16,
  input  in_17,
  input  in_18,
  input  in_19,
  input  in_20,
  input  in_21,
  input  in_22,
  input  in_23,
  input  in_24,
  input  in_25,
  input  in_26,
  input  in_27,
  input  in_28,
  input  in_29,
  input  in_30,
  input  in_31,
  input  in_32,
  output out_33,
  output out_34,
  output out_35,
  output out_36,
  output out_37,
  output out_38,
  output out_39,
  output out_40,
  output out_41,
  output out_42,
  output out_43,
  output out_44,
  output out_45,
  output out_46,
  output out_47,
  output out_48
);

  OR or_1 (.in_1(in_1), .in_2(in_17), .out_3(out_33));
  OR or_2 (.in_1(in_2), .in_2(in_18), .out_3(out_34));
  OR or_3 (.in_1(in_3), .in_2(in_19), .out_3(out_35));
  OR or_4 (.in_1(in_4), .in_2(in_20), .out_3(out_36));
  OR or_5 (.in_1(in_5), .in_2(in_21), .out_3(out_37));
  OR or_6 (.in_1(in_6), .in_2(in_22), .out_3(out_38));
  OR or_7 (.in_1(in_7), .in_2(in_23), .out_3(out_39));
  OR or_8 (.in_1(in_8), .in_2(in_24), .out_3(out_40));
  OR or_9 (.in_1(in_9), .in_2(in_25), .out_3(out_41));
  OR or_10 (.in_1(in_10), .in_2(in_26), .out_3(out_42));
  OR or_11 (.in_1(in_11), .in_2(in_27), .out_3(out_43));
  OR or_12 (.in_1(in_12), .in_2(in_28), .out_3(out_44));
  OR or_13 (.in_1(in_13), .in_2(in_29), .out_3(out_45));
  OR or_14 (.in_1(in_14), .in_2(in_30), .out_3(out_46));
  OR or_15 (.in_1(in_15), .in_2(in_31), .out_3(out_47));
  OR or_16 (.in_1(in_16), .in_2(in_32), .out_3(out_48));
endmodule

module Or8Way (
  input  in_1,
  input  in_2,
  input  in_3,
  input  in_4,
  input  in_5,
  input  in_6,
  input  in_7,
  input  in_8,
  output out_9
);

  wire or_1_out_3, or_2_out_3, or_3_out_3, or_4_out_3, or_5_out_3, or_6_out_3;

  OR or_1 (.in_1(in_1), .in_2(in_2), .out_3(or_1_out_3));
  OR or_2 (.in_1(in_3), .in_2(in_4), .out_3(or_2_out_3));
  OR or_3 (.in_1(in_5), .in_2(in_6), .out_3(or_3_out_3));
  OR or_4 (.in_1(in_7), .in_2(in_8), .out_3(or_4_out_3));
  OR or_5 (.in_1(or_1_out_3), .in_2(or_2_out_3), .out_3(or_5_out_3));
  OR or_6 (.in_1(or_3_out_3), .in_2(or_4_out_3), .out_3(or_6_out_3));
  OR or_7 (.in_1(or_5_out_3), .in_2(or_6_out_3), .out_3(out_9));
endmodule

module NOR (
  input  in_1,
  input  in_2,
  output out_3
);

  wire not_1_out_2, not_2_out_2;

  Not not_1 (.in_1(in_1), .out_2(not_1_out_2));
  Not not_2 (.in_1(in_2), .out_2(not_2_out_2));
  AND and_1 (.in_1(not_1_out_2), .in_2(not_2_out_2), .out_3(out_3));
endmodule

module _3NOR (
  input  in_1,
  input  in_2,
  input  in_3,
  output out_4
);

  wire not_1_out_2, not_2_out_2, not_3_out_2;

  Not not_1 (.in_1(in_1), .out_2(not_1_out_2));
  Not not_2 (.in_1(in_2), .out_2(not_2_out_2));
  Not not_3 (.in_1(in_3), .out_2(not_3_out_2));
  _3AND u_3and_1 (.in_1(not_1_out_2), .in_2(not_2_out_2), .in_3(not_3_out_2), .out_4(out_4));
endmodule

module Not (
  input  in_1,
  output out_2
);

  nand nand_1 (out_2, in_1, in_1);
endmodule

module Not16 (
  input  in_1,
  input  in_2,
  input  in_3,
  input  in_4,
  input  in_5,
  input  in_6,
  input  in_7,
  input  in_8,
  input  in_9,
  input  in_10,
  input  in_11,
  input  in_12,
  input  in_13,
  input  in_14,
  input  in_15,
  input  in_16,
  output out_17,
  output out_18,
  output out_19,
  output out_20,
  output out_21,
  output out_22,
  output out_23,
  output out_24,
  output out_25,
  output out_26,
  output out_27,
  output out_28,
  output out_29,
  output out_30,
  output out_31,
  output out_32
);

  Not not_1 (.in_1(in_1), .out_2(out_17));
  Not not_2 (.in_1(in_2), .out_2(out_18));
  Not not_3 (.in_1(in_3), .out_2(out_19));
  Not not_4 (.in_1(in_4), .out_2(out_20));
  Not not_5 (.in_1(in_5), .out_2(out_21));
  Not not_6 (.in_1(in_6), .out_2(out_22));
  Not not_7 (.in_1(in_7), .out_2(out_23));
  Not not_8 (.in_1(in_8), .out_2(out_24));
  Not not_9 (.in_1(in_9), .out_2(out_25));
  Not not_10 (.in_1(in_10), .out_2(out_26));
  Not not_11 (.in_1(in_11), .out_2(out_27));
  Not not_12 (.in_1(in_12), .out_2(out_28));
  Not not_13 (.in_1(in_13), .out_2(out_29));
  Not not_14 (.in_1(in_14), .out_2(out_30));
  Not not_15 (.in_1(in_15), .out_2(out_31));
  Not not_16 (.in_1(in_16), .out_2(out_32));
endmodule

module Xor (
  input  in_1,
  input  in_2,
  output out_3
);

  wire nand_1_out, or_1_out_3;

  OR or_1 (.in_1(in_1), .in_2(in_2), .out_3(or_1_out_3));
  nand nand_1 (nand_1_out, in_1, in_2);
  AND and_1 (.in_1(or_1_out_3), .in_2(nand_1_out), .out_3(out_3));
endmodule

module DMux (
  input  in_1,
  input  in_2,
  output out_3,
  output out_4
);

  wire not_1_out_2;

  Not not_1 (.in_1(in_1), .out_2(not_1_out_2));
  AND and_1 (.in_1(not_1_out_2), .in_2(in_2), .out_3(out_3));
  AND and_2 (.in_1(in_1), .in_2(in_2), .out_3(out_4));
endmodule

module DMux4Way (
  input  in_1,
  input  in_2,
  input  in_3,
  output out_4,
  output out_5,
  output out_6,
  output out_7
);

  wire and_1_out_3, and_2_out_3, and_3_out_3, and_4_out_3, not_1_out_2, not_2_out_2;

  Not not_1 (.in_1(in_1), .out_2(not_1_out_2));
  Not not_2 (.in_1(in_2), .out_2(not_2_out_2));
  AND and_1 (.in_1(not_1_out_2), .in_2(not_2_out_2), .out_3(and_1_out_3));
  AND and_2 (.in_1(not_1_out_2), .in_2(in_2), .out_3(and_2_out_3));
  AND and_3 (.in_1(in_1), .in_2(not_2_out_2), .out_3(and_3_out_3));
  AND and_4 (.in_1(in_1), .in_2(in_2), .out_3(and_4_out_3));
  AND and_5 (.in_1(and_1_out_3), .in_2(in_3), .out_3(out_4));
  AND and_6 (.in_1(and_2_out_3), .in_2(in_3), .out_3(out_5));
  AND and_7 (.in_1(and_3_out_3), .in_2(in_3), .out_3(out_6));
  AND and_8 (.in_1(and_4_out_3), .in_2(in_3), .out_3(out_7));

  // Notes on the sheet:
  //   sel-0
  //   sel-1
endmodule

module DMux8Way (
  input  in_1,
  input  in_2,
  input  in_3,
  input  in_4,
  output out_5,
  output out_6,
  output out_7,
  output out_8,
  output out_9,
  output out_10,
  output out_11,
  output out_12
);

  wire dmux_1_out_3, dmux_1_out_4;

  DMux dmux_1 (.in_1(in_1), .in_2(in_4), .out_3(dmux_1_out_3), .out_4(dmux_1_out_4));
  DMux4Way dmux4way_1 (
    .out_4(out_5), .out_5(out_6), .out_6(out_7), .out_7(out_8), .in_1(in_2), .in_2(in_3), .in_3(dmux_1_out_3));
  DMux4Way dmux4way_2 (
    .out_4(out_9), .out_5(out_10), .out_6(out_11), .out_7(out_12), .in_1(in_2), .in_2(in_3),
    .in_3(dmux_1_out_4));
endmodule

module Mux (
  input  in_1,
  input  in_2,
  input  in_3,
  output out_4
);

  wire and_1_out_3, and_2_out_3, not_1_out_2;

  Not not_1 (.in_1(in_1), .out_2(not_1_out_2));
  AND and_1 (.in_1(not_1_out_2), .in_2(in_2), .out_3(and_1_out_3));
  AND and_2 (.in_1(in_1), .in_2(in_3), .out_3(and_2_out_3));
  OR or_1 (.in_1(and_1_out_3), .in_2(and_2_out_3), .out_3(out_4));
endmodule

module Mux16 (
  input  in_1,
  input  in_2,
  input  in_3,
  input  in_4,
  input  in_5,
  input  in_6,
  input  in_7,
  input  in_8,
  input  in_9,
  input  in_10,
  input  in_11,
  input  in_12,
  input  in_13,
  input  in_14,
  input  in_15,
  input  in_16,
  input  in_17,
  input  in_18,
  input  in_19,
  input  in_20,
  input  in_21,
  input  in_22,
  input  in_23,
  input  in_24,
  input  in_25,
  input  in_26,
  input  in_27,
  input  in_28,
  input  in_29,
  input  in_30,
  input  in_31,
  input  in_32,
  input  in_33,
  output out_34,
  output out_35,
  output out_36,
  output out_37,
  output out_38,
  output out_39,
  output out_40,
  output out_41,
  output out_42,
  output out_43,
  output out_44,
  output out_45,
  output out_46,
  output out_47,
  output out_48,
  output out_49
);

  wire and16_1_out_33, and16_1_out_34, and16_1_out_35, and16_1_out_36, and16_1_out_37, and16_1_out_38,
       and16_1_out_39, and16_1_out_40, and16_1_out_41, and16_1_out_42, and16_1_out_43, and16_1_out_44,
       and16_1_out_45, and16_1_out_46, and16_1_out_47, and16_1_out_48, and16_2_out_33, and16_2_out_34,
       and16_2_out_35, and16_2_out_36, and16_2_out_37, and16_2_out_38, and16_2_out_39, and16_2_out_40,
       and16_2_out_41, and16_2_out_42, and16_2_out_43, and16_2_out_44, and16_2_out_45, and16_2_out_46,
       and16_2_out_47, and16_2_out_48, not_1_out_2;

  Not not_1 (.in_1(in_1), .out_2(not_1_out_2));
  AND16 and16_1 (
    .in_1(in_2), .in_2(in_3), .in_3(in_4), .in_4(in_5), .in_5(in_6), .in_6(in_7), .in_7(in_8), .in_8(in_9),
    .in_9(in_10), .in_10(in_11), .in_11(in_12), .in_12(in_13), .in_13(in_14), .in_14(in_15), .in_15(in_16),
    .in_16(in_17), .in_17(not_1_out_2), .in_18(not_1_out_2), .in_19(not_1_out_2), .in_20(not_1_out_2),
    .in_21(not_1_out_2), .in_22(not_1_out_2), .in_23(not_1_out_2), .in_24(not_1_out_2), .in_25(not_1_out_2),
    .in_26(not_1_out_2), .in_27(not_1_out_2), .in_28(not_1_out_2), .in_29(not_1_out_2), .in_30(not_1_out_2),
    .in_31(not_1_out_2), .in_32(not_1_out_2), .out_33(and16_1_out_33), .out_34(and16_1_out_34),
    .out_35(and16_1_out_35), .out_36(and16_1_out_36), .out_37(and16_1_out_37), .out_38(and16_1_out_38),
    .out_39(and16_1_out_39), .out_40(and16_1_out_40), .out_41(and16_1_out_41), .out_42(and16_1_out_42),
    .out_43(and16_1_out_43), .out_44(and16_1_out_44), .out_45(and16_1_out_45), .out_46(and16_1_out_46),
    .out_47(and16_1_out_47), .out_48(and16_1_out_48));
  AND16 and16_2 (
    .in_1(in_18), .in_2(in_19), .in_3(in_20), .in_4(in_21), .in_5(in_22), .in_6(in_23), .in_7(in_24),
    .in_8(in_25), .in_9(in_26), .in_10(in_27), .in_11(in_28), .in_12(in_29), .in_13(in_30), .in_14(in_31),
    .in_15(in_32), .in_16(in_33), .in_17(in_1), .in_18(in_1), .in_19(in_1), .in_20(in_1), .in_21(in_1),
    .in_22(in_1), .in_23(in_1), .in_24(in_1), .in_25(in_1), .in_26(in_1), .in_27(in_1), .in_28(in_1),
    .in_29(in_1), .in_30(in_1), .in_31(in_1), .in_32(in_1), .out_33(and16_2_out_33), .out_34(and16_2_out_34),
    .out_35(and16_2_out_35), .out_36(and16_2_out_36), .out_37(and16_2_out_37), .out_38(and16_2_out_38),
    .out_39(and16_2_out_39), .out_40(and16_2_out_40), .out_41(and16_2_out_41), .out_42(and16_2_out_42),
    .out_43(and16_2_out_43), .out_44(and16_2_out_44), .out_45(and16_2_out_45), .out_46(and16_2_out_46),
    .out_47(and16_2_out_47), .out_48(and16_2_out_48));
  OR16 or16_1 (
    .in_1(and16_1_out_33), .in_2(and16_1_out_34), .in_3(and16_1_out_35), .in_4(and16_1_out_36),
    .in_5(and16_1_out_37), .in_6(and16_1_out_38), .in_7(and16_1_out_39), .in_8(and16_1_out_40),
    .in_9(and16_1_out_41), .in_10(and16_1_out_42), .in_11(and16_1_out_43), .in_12(and16_1_out_44),
    .in_13(and16_1_out_45), .in_14(and16_1_out_46), .in_15(and16_1_out_47), .in_16(and16_1_out_48),
    .in_17(and16_2_out_33), .in_18(and16_2_out_34), .in_19(and16_2_out_35), .in_20(and16_2_out_36),
    .in_21(and16_2_out_37), .in_22(and16_2_out_38), .in_23(and16_2_out_39), .in_24(and16_2_out_40),
    .in_25(and16_2_out_41), .in_26(and16_2_out_42), .in_27(and16_2_out_43), .in_28(and16_2_out_44),
    .in_29(and16_2_out_45), .in_30(and16_2_out_46), .in_31(and16_2_out_47), .in_32(and16_2_out_48),
    .out_33(out_34), .out_34(out_35), .out_35(out_36), .out_36(out_37), .out_37(out_38), .out_38(out_39),
    .out_39(out_40), .out_40(out_41), .out_41(out_42), .out_42(out_43), .out_43(out_44), .out_44(out_45),
    .out_45(out_46), .out_46(out_47), .out_47(out_48), .out_48(out_49));
endmodule

module Mux4Way16 (
  input  in_1,
  input  in_2,
  input  in_3,
  input  in_4,
  input  in_5,
  input  in_6,
  input  in_7,
  input  in_8,
  input  in_9,
  input  in_10,
  input  in_11,
  input  in_12,
  input  in_13,
  input  in_14,
  input  in_15,
  input  in_16,
  input  in_17,
  input  in_18,
  input  in_19,
  input  in_20,
  input  in_21,
  input  in_22,
  input  in_23,
  input  in_24,
  input  in_25,
  input  in_26,
  input  in_27,
  input  in_28,
  input  in_29,
  input  in_30,
  input  in_31,
  input  in_32,
  input  in_33,
  input  in_34,
  input  in_35,
  input  in_36,
  input  in_37,
  input  in_38,
  input  in_39,
  input  in_40,
  input  in_41,
  input  in_42,
  input  in_43,
  input  in_44,
  input  in_45,
  input  in_46,
  input  in_47,
  input  in_48,
  input  in_49,
  input  in_50,
  input  in_51,
  input  in_52,
  input  in_53,
  input  in_54,
  input  in_55,
  input  in_56,
  input  in_57,
  input  in_58,
  input  in_59,
  input  in_60,
  input  in_61,
  input  in_62,
  input  in_63,
  input  in_64,
  input  in_65,
  input  in_66,
  output out_67,
  output out_68,
  output out_69,
  output out_70,
  output out_71,
  output out_72,
  output out_73,
  output out_74,
  output out_75,
  output out_76,
  output out_77,
  output out_78,
  output out_79,
  output out_80,
  output out_81,
  output out_82
);

  wire and16_1_out_33, and16_1_out_34, and16_1_out_35, and16_1_out_36, and16_1_out_37, and16_1_out_38,
       and16_1_out_39, and16_1_out_40, and16_1_out_41, and16_1_out_42, and16_1_out_43, and16_1_out_44,
       and16_1_out_45, and16_1_out_46, and16_1_out_47, and16_1_out_48, and16_2_out_33, and16_2_out_34,
       and16_2_out_35, and16_2_out_36, and16_2_out_37, and16_2_out_38, and16_2_out_39, and16_2_out_40,
       and16_2_out_41, and16_2_out_42, and16_2_out_43, and16_2_out_44, and16_2_out_45, and16_2_out_46,
       and16_2_out_47, and16_2_out_48, mux16_1_out_34, mux16_1_out_35, mux16_1_out_36, mux16_1_out_37,
       mux16_1_out_38, mux16_1_out_39, mux16_1_out_40, mux16_1_out_41, mux16_1_out_42, mux16_1_out_43,
       mux16_1_out_44, mux16_1_out_45, mux16_1_out_46, mux16_1_out_47, mux16_1_out_48, mux16_1_out_49,
       mux16_2_out_34, mux16_2_out_35, mux16_2_out_36, mux16_2_out_37, mux16_2_out_38, mux16_2_out_39,
       mux16_2_out_40, mux16_2_out_41, mux16_2_out_42, mux16_2_out_43, mux16_2_out_44, mux16_2_out_45,
       mux16_2_out_46, mux16_2_out_47, mux16_2_out_48, mux16_2_out_49, not_1_out_2;

  Mux16 mux16_1 (
    .in_2(in_3), .in_3(in_4), .in_4(in_5), .in_5(in_6), .in_6(in_7), .in_7(in_8), .in_8(in_9), .in_9(in_10),
    .in_10(in_11), .in_11(in_12), .in_12(in_13), .in_13(in_14), .in_14(in_15), .in_15(in_16), .in_16(in_17),
    .in_17(in_18), .in_18(in_19), .in_19(in_20), .in_20(in_21), .in_21(in_22), .in_22(in_23), .in_23(in_24),
    .in_24(in_25), .in_25(in_26), .in_26(in_27), .in_27(in_28), .in_28(in_29), .in_29(in_30), .in_30(in_31),
    .in_31(in_32), .in_32(in_33), .in_33(in_34), .out_34(mux16_1_out_34), .out_35(mux16_1_out_35),
    .out_36(mux16_1_out_36), .out_37(mux16_1_out_37), .out_38(mux16_1_out_38), .out_39(mux16_1_out_39),
    .out_40(mux16_1_out_40), .out_41(mux16_1_out_41), .out_42(mux16_1_out_42), .out_43(mux16_1_out_43),
    .out_44(mux16_1_out_44), .out_45(mux16_1_out_45), .out_46(mux16_1_out_46), .out_47(mux16_1_out_47),
    .out_48(mux16_1_out_48), .out_49(mux16_1_out_49), .in_1(in_2));
  Mux16 mux16_2 (
    .in_2(in_35), .in_3(in_36), .in_4(in_37), .in_5(in_38), .in_6(in_39), .in_7(in_40), .in_8(in_41),
    .in_9(in_42), .in_10(in_43), .in_11(in_44), .in_12(in_45), .in_13(in_46), .in_14(in_47), .in_15(in_48),
    .in_16(in_49), .in_17(in_50), .in_18(in_51), .in_19(in_52), .in_20(in_53), .in_21(in_54), .in_22(in_55),
    .in_23(in_56), .in_24(in_57), .in_25(in_58), .in_26(in_59), .in_27(in_60), .in_28(in_61), .in_29(in_62),
    .in_30(in_63), .in_31(in_64), .in_32(in_65), .in_33(in_66), .out_34(mux16_2_out_34),
    .out_35(mux16_2_out_35), .out_36(mux16_2_out_36), .out_37(mux16_2_out_37), .out_38(mux16_2_out_38),
    .out_39(mux16_2_out_39), .out_40(mux16_2_out_40), .out_41(mux16_2_out_41), .out_42(mux16_2_out_42),
    .out_43(mux16_2_out_43), .out_44(mux16_2_out_44), .out_45(mux16_2_out_45), .out_46(mux16_2_out_46),
    .out_47(mux16_2_out_47), .out_48(mux16_2_out_48), .out_49(mux16_2_out_49), .in_1(in_2));
  Not not_1 (.in_1(in_1), .out_2(not_1_out_2));
  AND16 and16_1 (
    .in_1(mux16_1_out_34), .in_2(mux16_1_out_35), .in_3(mux16_1_out_36), .in_4(mux16_1_out_37),
    .in_5(mux16_1_out_38), .in_6(mux16_1_out_39), .in_7(mux16_1_out_40), .in_8(mux16_1_out_41),
    .in_9(mux16_1_out_42), .in_10(mux16_1_out_43), .in_11(mux16_1_out_44), .in_12(mux16_1_out_45),
    .in_13(mux16_1_out_46), .in_14(mux16_1_out_47), .in_15(mux16_1_out_48), .in_16(mux16_1_out_49),
    .in_17(not_1_out_2), .in_18(not_1_out_2), .in_19(not_1_out_2), .in_20(not_1_out_2), .in_21(not_1_out_2),
    .in_22(not_1_out_2), .in_23(not_1_out_2), .in_24(not_1_out_2), .in_25(not_1_out_2), .in_26(not_1_out_2),
    .in_27(not_1_out_2), .in_28(not_1_out_2), .in_29(not_1_out_2), .in_30(not_1_out_2), .in_31(not_1_out_2),
    .in_32(not_1_out_2), .out_33(and16_1_out_33), .out_34(and16_1_out_34), .out_35(and16_1_out_35),
    .out_36(and16_1_out_36), .out_37(and16_1_out_37), .out_38(and16_1_out_38), .out_39(and16_1_out_39),
    .out_40(and16_1_out_40), .out_41(and16_1_out_41), .out_42(and16_1_out_42), .out_43(and16_1_out_43),
    .out_44(and16_1_out_44), .out_45(and16_1_out_45), .out_46(and16_1_out_46), .out_47(and16_1_out_47),
    .out_48(and16_1_out_48));
  AND16 and16_2 (
    .in_1(mux16_2_out_34), .in_2(mux16_2_out_35), .in_3(mux16_2_out_36), .in_4(mux16_2_out_37),
    .in_5(mux16_2_out_38), .in_6(mux16_2_out_39), .in_7(mux16_2_out_40), .in_8(mux16_2_out_41),
    .in_9(mux16_2_out_42), .in_10(mux16_2_out_43), .in_11(mux16_2_out_44), .in_12(mux16_2_out_45),
    .in_13(mux16_2_out_46), .in_14(mux16_2_out_47), .in_15(mux16_2_out_48), .in_16(mux16_2_out_49),
    .in_17(in_1), .in_18(in_1), .in_19(in_1), .in_20(in_1), .in_21(in_1), .in_22(in_1), .in_23(in_1),
    .in_24(in_1), .in_25(in_1), .in_26(in_1), .in_27(in_1), .in_28(in_1), .in_29(in_1), .in_30(in_1),
    .in_31(in_1), .in_32(in_1), .out_33(and16_2_out_33), .out_34(and16_2_out_34), .out_35(and16_2_out_35),
    .out_36(and16_2_out_36), .out_37(and16_2_out_37), .out_38(and16_2_out_38), .out_39(and16_2_out_39),
    .out_40(and16_2_out_40), .out_41(and16_2_out_41), .out_42(and16_2_out_42), .out_43(and16_2_out_43),
    .out_44(and16_2_out_44), .out_45(and16_2_out_45), .out_46(and16_2_out_46), .out_47(and16_2_out_47),
    .out_48(and16_2_out_48));
  OR16 or16_1 (
    .in_1(and16_1_out_33), .in_2(and16_1_out_34), .in_3(and16_1_out_35), .in_4(and16_1_out_36),
    .in_5(and16_1_out_37), .in_6(and16_1_out_38), .in_7(and16_1_out_39), .in_8(and16_1_out_40),
    .in_9(and16_1_out_41), .in_10(and16_1_out_42), .in_11(and16_1_out_43), .in_12(and16_1_out_44),
    .in_13(and16_1_out_45), .in_14(and16_1_out_46), .in_15(and16_1_out_47), .in_16(and16_1_out_48),
    .in_17(and16_2_out_33), .in_18(and16_2_out_34), .in_19(and16_2_out_35), .in_20(and16_2_out_36),
    .in_21(and16_2_out_37), .in_22(and16_2_out_38), .in_23(and16_2_out_39), .in_24(and16_2_out_40),
    .in_25(and16_2_out_41), .in_26(and16_2_out_42), .in_27(and16_2_out_43), .in_28(and16_2_out_44),
    .in_29(and16_2_out_45), .in_30(and16_2_out_46), .in_31(and16_2_out_47), .in_32(and16_2_out_48),
    .out_33(out_67), .out_34(out_68), .out_35(out_69), .out_36(out_70), .out_37(out_71), .out_38(out_72),
    .out_39(out_73), .out_40(out_74), .out_41(out_75), .out_42(out_76), .out_43(out_77), .out_44(out_78),
    .out_45(out_79), .out_46(out_80), .out_47(out_81), .out_48(out_82));
endmodule

module Mux8Way16 (
  input  in_1,
  input  in_2,
  input  in_3,
  input  in_4,
  input  in_5,
  input  in_6,
  input  in_7,
  input  in_8,
  input  in_9,
  input  in_10,
  input  in_11,
  input  in_12,
  input  in_13,
  input  in_14,
  input  in_15,
  input  in_16,
  input  in_17,
  input  in_18,
  input  in_19,
  input  in_20,
  input  in_21,
  input  in_22,
  input  in_23,
  input  in_24,
  input  in_25,
  input  in_26,
  input  in_27,
  input  in_28,
  input  in_29,
  input  in_30,
  input  in_31,
  input  in_32,
  input  in_33,
  input  in_34,
  input  in_35,
  input  in_36,
  input  in_37,
  input  in_38,
  input  in_39,
  input  in_40,
  input  in_41,
  input  in_42,
  input  in_43,
  input  in_44,
  input  in_45,
  input  in_46,
  input  in_47,
  input  in_48,
  input  in_49,
  input  in_50,
  input  in_51,
  input  in_52,
  input  in_53,
  input  in_54,
  input  in_55,
  input  in_56,
  input  in_57,
  input  in_58,
  input  in_59,
  input  in_60,
  input  in_61,
  input  in_62,
  input  in_63,
  input  in_64,
  input  in_65,
  input  in_66,
  input  in_67,
  input  in_68,
  input  in_69,
  input  in_70,
  input  in_71,
  input  in_72,
  input  in_73,
  input  in_74,
  input  in_75,
  input  in_76,
  input  in_77,
  input  in_78,
  input  in_79,
  input  in_80,
  input  in_81,
  input  in_82,
  input  in_83,
  input  in_84,
  input  in_85,
  input  in_86,
  input  in_87,
  input  in_88,
  input  in_89,
  input  in_90,
  input  in_91,
  input  in_92,
  input  in_93,
  input  in_94,
  input  in_95,
  input  in_96,
  input  in_97,
  input  in_98,
  input  in_99,
  input  in_100,
  input  in_101,
  input  in_102,
  input  in_103,
  input  in_104,
  input  in_105,
  input  in_106,
  input  in_107,
  input  in_108,
  input  in_109,
  input  in_110,
  input  in_111,
  input  in_112,
  input  in_113,
  input  in_114,
  input  in_115,
  input  in_116,
  input  in_117,
  input  in_118,
  input  in_119,
  input  in_120,
  input  in_121,
  input  in_122,
  input  in_123,
  input  in_124,
  input  in_125,
  input  in_126,
  input  in_127,
  input  in_128,
  input  in_129,
  input  in_130,
  input  in_131,
  output out_132,
  output out_133,
  output out_134,
  output out_135,
  output out_136,
  output out_137,
  output out_138,
  output out_139,
  output out_140,
  output out_141,
  output out_142,
  output out_143,
  output out_144,
  output out_145,
  output out_146,
  output out_147
);

  wire mux4way16_1_out_67, mux4way16_1_out_68, mux4way16_1_out_69, mux4way16_1_out_70, mux4way16_1_out_71,
       mux4way16_1_out_72, mux4way16_1_out_73, mux4way16_1_out_74, mux4way16_1_out_75, mux4way16_1_out_76,
       mux4way16_1_out_77, mux4way16_1_out_78, mux4way16_1_out_79, mux4way16_1_out_80, mux4way16_1_out_81,
       mux4way16_1_out_82, mux4way16_2_out_67, mux4way16_2_out_68, mux4way16_2_out_69, mux4way16_2_out_70,
       mux4way16_2_out_71, mux4way16_2_out_72, mux4way16_2_out_73, mux4way16_2_out_74, mux4way16_2_out_75,
       mux4way16_2_out_76, mux4way16_2_out_77, mux4way16_2_out_78, mux4way16_2_out_79, mux4way16_2_out_80,
       mux4way16_2_out_81, mux4way16_2_out_82;

  Mux4Way16 mux4way16_1 (
    .in_3(in_4), .in_4(in_5), .in_5(in_6), .in_6(in_7), .in_7(in_8), .in_8(in_9), .in_9(in_10),
    .in_10(in_11), .in_11(in_12), .in_12(in_13), .in_13(in_14), .in_14(in_15), .in_15(in_16), .in_16(in_17),
    .in_17(in_18), .in_18(in_19), .in_19(in_20), .in_20(in_21), .in_21(in_22), .in_22(in_23), .in_23(in_24),
    .in_24(in_25), .in_25(in_26), .in_26(in_27), .in_27(in_28), .in_28(in_29), .in_29(in_30), .in_30(in_31),
    .in_31(in_32), .in_32(in_33), .in_33(in_34), .in_34(in_35), .in_35(in_36), .in_36(in_37), .in_37(in_38),
    .in_38(in_39), .in_39(in_40), .in_40(in_41), .in_41(in_42), .in_42(in_43), .in_43(in_44), .in_44(in_45),
    .in_45(in_46), .in_46(in_47), .in_47(in_48), .in_48(in_49), .in_49(in_50), .in_50(in_51), .in_51(in_52),
    .in_52(in_53), .in_53(in_54), .in_54(in_55), .in_55(in_56), .in_56(in_57), .in_57(in_58), .in_58(in_59),
    .in_59(in_60), .in_60(in_61), .in_61(in_62), .in_62(in_63), .in_63(in_64), .in_64(in_65), .in_65(in_66),
    .in_66(in_67), .out_67(mux4way16_1_out_67), .out_68(mux4way16_1_out_68), .out_69(mux4way16_1_out_69),
    .out_70(mux4way16_1_out_70), .out_71(mux4way16_1_out_71), .out_72(mux4way16_1_out_72),
    .out_73(mux4way16_1_out_73), .out_74(mux4way16_1_out_74), .out_75(mux4way16_1_out_75),
    .out_76(mux4way16_1_out_76), .out_77(mux4way16_1_out_77), .out_78(mux4way16_1_out_78),
    .out_79(mux4way16_1_out_79), .out_80(mux4way16_1_out_80), .out_81(mux4way16_1_out_81),
    .out_82(mux4way16_1_out_82), .in_2(in_3), .in_1(in_2));
  Mux4Way16 mux4way16_2 (
    .in_3(in_68), .in_4(in_69), .in_5(in_70), .in_6(in_71), .in_7(in_72), .in_8(in_73), .in_9(in_74),
    .in_10(in_75), .in_11(in_76), .in_12(in_77), .in_13(in_78), .in_14(in_79), .in_15(in_80), .in_16(in_81),
    .in_17(in_82), .in_18(in_83), .in_19(in_84), .in_20(in_85), .in_21(in_86), .in_22(in_87), .in_23(in_88),
    .in_24(in_89), .in_25(in_90), .in_26(in_91), .in_27(in_92), .in_28(in_93), .in_29(in_94), .in_30(in_95),
    .in_31(in_96), .in_32(in_97), .in_33(in_98), .in_34(in_99), .in_35(in_100), .in_36(in_101),
    .in_37(in_102), .in_38(in_103), .in_39(in_104), .in_40(in_105), .in_41(in_106), .in_42(in_107),
    .in_43(in_108), .in_44(in_109), .in_45(in_110), .in_46(in_111), .in_47(in_112), .in_48(in_113),
    .in_49(in_114), .in_50(in_115), .in_51(in_116), .in_52(in_117), .in_53(in_118), .in_54(in_119),
    .in_55(in_120), .in_56(in_121), .in_57(in_122), .in_58(in_123), .in_59(in_124), .in_60(in_125),
    .in_61(in_126), .in_62(in_127), .in_63(in_128), .in_64(in_129), .in_65(in_130), .in_66(in_131),
    .out_67(mux4way16_2_out_67), .out_68(mux4way16_2_out_68), .out_69(mux4way16_2_out_69),
    .out_70(mux4way16_2_out_70), .out_71(mux4way16_2_out_71), .out_72(mux4way16_2_out_72),
    .out_73(mux4way16_2_out_73), .out_74(mux4way16_2_out_74), .out_75(mux4way16_2_out_75),
    .out_76(mux4way16_2_out_76), .out_77(mux4way16_2_out_77), .out_78(mux4way16_2_out_78),
    .out_79(mux4way16_2_out_79), .out_80(mux4way16_2_out_80), .out_81(mux4way16_2_out_81),
    .out_82(mux4way16_2_out_82));  // open: in_2, in_1
  Mux16 mux16_1 (
    .in_2(mux4way16_1_out_67), .in_3(mux4way16_1_out_68), .in_4(mux4way16_1_out_69),
    .in_5(mux4way16_1_out_70), .in_6(mux4way16_1_out_71), .in_7(mux4way16_1_out_72),
    .in_8(mux4way16_1_out_73), .in_9(mux4way16_1_out_74), .in_10(mux4way16_1_out_75),
    .in_11(mux4way16_1_out_76), .in_12(mux4way16_1_out_77), .in_13(mux4way16_1_out_78),
    .in_14(mux4way16_1_out_79), .in_15(mux4way16_1_out_80), .in_16(mux4way16_1_out_81),
    .in_17(mux4way16_1_out_82), .in_18(mux4way16_2_out_67), .in_19(mux4way16_2_out_68),
    .in_20(mux4way16_2_out_69), .in_21(mux4way16_2_out_70), .in_22(mux4way16_2_out_71),
    .in_23(mux4way16_2_out_72), .in_24(mux4way16_2_out_73), .in_25(mux4way16_2_out_74),
    .in_26(mux4way16_2_out_75), .in_27(mux4way16_2_out_76), .in_28(mux4way16_2_out_77),
    .in_29(mux4way16_2_out_78), .in_30(mux4way16_2_out_79), .in_31(mux4way16_2_out_80),
    .in_32(mux4way16_2_out_81), .in_33(mux4way16_2_out_82), .out_34(out_132), .out_35(out_133),
    .out_36(out_134), .out_37(out_135), .out_38(out_136), .out_39(out_137), .out_40(out_138),
    .out_41(out_139), .out_42(out_140), .out_43(out_141), .out_44(out_142), .out_45(out_143),
    .out_46(out_144), .out_47(out_145), .out_48(out_146), .out_49(out_147), .in_1(in_1));
endmodule

module HalfAdder (
  input  in_1,
  input  in_2,
  output out_3,
  output out_4
);

  Xor xor_1 (.in_1(in_1), .in_2(in_2), .out_3(out_3));
  AND and_1 (.in_1(in_1), .in_2(in_2), .out_3(out_4));
endmodule

module FullAdder (
  input  in_1,
  input  in_2,
  input  in_3,
  output out_4,
  output out_5
);

  wire halfadder_1_out_3, halfadder_1_out_4, halfadder_2_out_4;

  HalfAdder halfadder_1 (.in_1(in_2), .in_2(in_3), .out_3(halfadder_1_out_3), .out_4(halfadder_1_out_4));
  HalfAdder halfadder_2 (.in_1(in_1), .in_2(halfadder_1_out_3), .out_3(out_4), .out_4(halfadder_2_out_4));
  OR or_1 (.in_1(halfadder_2_out_4), .in_2(halfadder_1_out_4), .out_3(out_5));
endmodule

module ADD16 (
  input  in_1,
  input  in_2,
  input  in_3,
  input  in_4,
  input  in_5,
  input  in_6,
  input  in_7,
  input  in_8,
  input  in_9,
  input  in_10,
  input  in_11,
  input  in_12,
  input  in_13,
  input  in_14,
  input  in_15,
  input  in_16,
  input  in_17,
  input  in_18,
  input  in_19,
  input  in_20,
  input  in_21,
  input  in_22,
  input  in_23,
  input  in_24,
  input  in_25,
  input  in_26,
  input  in_27,
  input  in_28,
  input  in_29,
  input  in_30,
  input  in_31,
  input  in_32,
  input  in_33,
  output out_34,
  output out_35,
  output out_36,
  output out_37,
  output out_38,
  output out_39,
  output out_40,
  output out_41,
  output out_42,
  output out_43,
  output out_44,
  output out_45,
  output out_46,
  output out_47,
  output out_48,
  output out_49
);

  wire fulladder_1_out_5, fulladder_2_out_5, fulladder_3_out_5, fulladder_4_out_5, fulladder_5_out_5,
       fulladder_6_out_5, fulladder_7_out_5, fulladder_8_out_5, fulladder_9_out_5, fulladder_10_out_5,
       fulladder_11_out_5, fulladder_12_out_5, fulladder_13_out_5, fulladder_14_out_5, fulladder_15_out_5,
       fulladder_16_out_5;

  FullAdder fulladder_1 (.in_1(in_1), .in_2(in_2), .in_3(in_3), .out_4(out_34), .out_5(fulladder_1_out_5));
  FullAdder fulladder_2 (.in_1(fulladder_1_out_5), .in_2(in_4), .in_3(in_5), .out_4(out_35), .out_5(fulladder_2_out_5));
  FullAdder fulladder_3 (.in_1(fulladder_2_out_5), .in_2(in_6), .in_3(in_7), .out_4(out_36), .out_5(fulladder_3_out_5));
  FullAdder fulladder_4 (.in_1(fulladder_3_out_5), .in_2(in_8), .in_3(in_9), .out_4(out_37), .out_5(fulladder_4_out_5));
  FullAdder fulladder_5 (
    .in_1(fulladder_4_out_5), .in_2(in_10), .in_3(in_11), .out_4(out_38), .out_5(fulladder_5_out_5));
  FullAdder fulladder_6 (
    .in_1(fulladder_5_out_5), .in_2(in_12), .in_3(in_13), .out_4(out_39), .out_5(fulladder_6_out_5));
  FullAdder fulladder_7 (
    .in_1(fulladder_6_out_5), .in_2(in_14), .in_3(in_15), .out_4(out_40), .out_5(fulladder_7_out_5));
  FullAdder fulladder_8 (
    .in_1(fulladder_7_out_5), .in_2(in_16), .in_3(in_17), .out_4(out_41), .out_5(fulladder_8_out_5));
  FullAdder fulladder_9 (
    .in_1(fulladder_8_out_5), .in_2(in_18), .in_3(in_19), .out_4(out_42), .out_5(fulladder_9_out_5));
  FullAdder fulladder_10 (
    .in_1(fulladder_9_out_5), .in_2(in_20), .in_3(in_21), .out_4(out_43), .out_5(fulladder_10_out_5));
  FullAdder fulladder_11 (
    .in_1(fulladder_10_out_5), .in_2(in_22), .in_3(in_23), .out_4(out_44), .out_5(fulladder_11_out_5));
  FullAdder fulladder_12 (
    .in_1(fulladder_11_out_5), .in_2(in_24), .in_3(in_25), .out_4(out_45), .out_5(fulladder_12_out_5));
  FullAdder fulladder_13 (
    .in_1(fulladder_12_out_5), .in_2(in_26), .in_3(in_27), .out_4(out_46), .out_5(fulladder_13_out_5));
  FullAdder fulladder_14 (
    .in_1(fulladder_13_out_5), .in_2(in_28), .in_3(in_29), .out_4(out_47), .out_5(fulladder_14_out_5));
  FullAdder fulladder_15 (
    .in_1(fulladder_14_out_5), .in_2(in_30), .in_3(in_31), .out_4(out_48), .out_5(fulladder_15_out_5));
  FullAdder fulladder_16 (
    .in_1(fulladder_15_out_5), .in_2(in_32), .in_3(in_33), .out_4(out_49), .out_5(fulladder_16_out_5));
endmodule

module Inc16 (
  input  in_1,
  input  in_2,
  input  in_3,
  input  in_4,
  input  in_5,
  input  in_6,
  input  in_7,
  input  in_8,
  input  in_9,
  input  in_10,
  input  in_11,
  input  in_12,
  input  in_13,
  input  in_14,
  input  in_15,
  input  in_16,
  input  in_17,
  output out_18,
  output out_19,
  output out_20,
  output out_21,
  output out_22,
  output out_23,
  output out_24,
  output out_25,
  output out_26,
  output out_27,
  output out_28,
  output out_29,
  output out_30,
  output out_31,
  output out_32,
  output out_33
);

  ADD16 add16_1 (
    .in_2(in_1), .in_3(in_2), .in_4(in_3), .in_5(1'b0), .in_6(in_4), .in_7(1'b0), .in_8(in_5), .in_9(1'b0),
    .in_10(in_6), .in_11(1'b0), .in_12(in_7), .in_13(1'b0), .in_14(in_8), .in_15(1'b0), .in_16(in_9),
    .in_17(1'b0), .in_18(in_10), .in_19(1'b0), .in_20(in_11), .in_21(1'b0), .in_22(in_12), .in_23(1'b0),
    .in_24(in_13), .in_25(1'b0), .in_26(in_14), .in_27(1'b0), .in_28(in_15), .in_29(1'b0), .in_30(in_16),
    .in_31(1'b0), .in_32(in_17), .in_33(1'b0), .out_34(out_18), .out_35(out_19), .out_36(out_20),
    .out_37(out_21), .out_38(out_22), .out_39(out_23), .out_40(out_24), .out_41(out_25), .out_42(out_26),
    .out_43(out_27), .out_44(out_28), .out_45(out_29), .out_46(out_30), .out_47(out_31), .out_48(out_32),
    .out_49(out_33), .in_1(1'b0));
endmodule

module ALU (
  input  in_1,
  input  in_2,
  input  in_3,
  input  in_4,
  input  in_5,
  input  in_6,
  input  in_7,
  input  in_8,
  input  in_9,
  input  in_10,
  input  in_11,
  input  in_12,
  input  in_13,
  input  in_14,
  input  in_15,
  input  in_16,
  input  in_17,
  input  in_18,
  input  in_19,
  input  in_20,
  input  in_21,
  input  in_22,
  input  in_23,
  input  in_24,
  input  in_25,
  input  in_26,
  input  in_27,
  input  in_28,
  input  in_29,
  input  in_30,
  input  in_31,
  input  in_32,
  input  in_33,
  input  in_34,
  input  in_35,
  input  in_36,
  input  in_37,
  input  in_38,
  output out_39,
  output out_40,
  output out_41,
  output out_42,
  output out_43,
  output out_44,
  output out_45,
  output out_46,
  output out_47,
  output out_48,
  output out_49,
  output out_50,
  output out_51,
  output out_52,
  output out_53,
  output out_54,
  output out_55,
  output out_56
);

  wire add16_1_out_34, add16_1_out_35, add16_1_out_36, add16_1_out_37, add16_1_out_38, add16_1_out_39,
       add16_1_out_40, add16_1_out_41, add16_1_out_42, add16_1_out_43, add16_1_out_44, add16_1_out_45,
       add16_1_out_46, add16_1_out_47, add16_1_out_48, add16_1_out_49, and16_1_out_33, and16_1_out_34,
       and16_1_out_35, and16_1_out_36, and16_1_out_37, and16_1_out_38, and16_1_out_39, and16_1_out_40,
       and16_1_out_41, and16_1_out_42, and16_1_out_43, and16_1_out_44, and16_1_out_45, and16_1_out_46,
       and16_1_out_47, and16_1_out_48, mux16_1_out_34, mux16_1_out_35, mux16_1_out_36, mux16_1_out_37,
       mux16_1_out_38, mux16_1_out_39, mux16_1_out_40, mux16_1_out_41, mux16_1_out_42, mux16_1_out_43,
       mux16_1_out_44, mux16_1_out_45, mux16_1_out_46, mux16_1_out_47, mux16_1_out_48, mux16_1_out_49,
       mux16_2_out_34, mux16_2_out_35, mux16_2_out_36, mux16_2_out_37, mux16_2_out_38, mux16_2_out_39,
       mux16_2_out_40, mux16_2_out_41, mux16_2_out_42, mux16_2_out_43, mux16_2_out_44, mux16_2_out_45,
       mux16_2_out_46, mux16_2_out_47, mux16_2_out_48, mux16_2_out_49, mux16_3_out_34, mux16_3_out_35,
       mux16_3_out_36, mux16_3_out_37, mux16_3_out_38, mux16_3_out_39, mux16_3_out_40, mux16_3_out_41,
       mux16_3_out_42, mux16_3_out_43, mux16_3_out_44, mux16_3_out_45, mux16_3_out_46, mux16_3_out_47,
       mux16_3_out_48, mux16_3_out_49, mux16_4_out_34, mux16_4_out_35, mux16_4_out_36, mux16_4_out_37,
       mux16_4_out_38, mux16_4_out_39, mux16_4_out_40, mux16_4_out_41, mux16_4_out_42, mux16_4_out_43,
       mux16_4_out_44, mux16_4_out_45, mux16_4_out_46, mux16_4_out_47, mux16_4_out_48, mux16_4_out_49,
       mux16_5_out_34, mux16_5_out_35, mux16_5_out_36, mux16_5_out_37, mux16_5_out_38, mux16_5_out_39,
       mux16_5_out_40, mux16_5_out_41, mux16_5_out_42, mux16_5_out_43, mux16_5_out_44, mux16_5_out_45,
       mux16_5_out_46, mux16_5_out_47, mux16_5_out_48, mux16_5_out_49, not16_1_out_17, not16_1_out_18,
       not16_1_out_19, not16_1_out_20, not16_1_out_21, not16_1_out_22, not16_1_out_23, not16_1_out_24,
       not16_1_out_25, not16_1_out_26, not16_1_out_27, not16_1_out_28, not16_1_out_29, not16_1_out_30,
       not16_1_out_31, not16_1_out_32, not16_2_out_17, not16_2_out_18, not16_2_out_19, not16_2_out_20,
       not16_2_out_21, not16_2_out_22, not16_2_out_23, not16_2_out_24, not16_2_out_25, not16_2_out_26,
       not16_2_out_27, not16_2_out_28, not16_2_out_29, not16_2_out_30, not16_2_out_31, not16_2_out_32,
       not16_3_out_17, not16_3_out_18, not16_3_out_19, not16_3_out_20, not16_3_out_21, not16_3_out_22,
       not16_3_out_23, not16_3_out_24, not16_3_out_25, not16_3_out_26, not16_3_out_27, not16_3_out_28,
       not16_3_out_29, not16_3_out_30, not16_3_out_31, not16_3_out_32, or8way_1_out_9, or8way_2_out_9,
       or_1_out_3;

  Mux16 mux16_1 (
    .in_2(in_3), .in_3(in_4), .in_4(in_5), .in_5(in_6), .in_6(in_7), .in_7(in_8), .in_8(in_9), .in_9(in_10),
    .in_10(in_11), .in_11(in_12), .in_12(in_13), .in_13(in_15), .in_14(in_16), .in_15(in_17), .in_16(in_18),
    .in_17(in_19), .in_18(1'b0), .in_19(1'b0), .in_20(1'b0), .in_21(1'b0), .in_22(1'b0), .in_23(1'b0),
    .in_24(1'b0), .in_25(1'b0), .in_26(1'b0), .in_27(1'b0), .in_28(1'b0), .in_29(1'b0), .in_30(1'b0),
    .in_31(1'b0), .in_32(1'b0), .in_33(1'b0), .out_34(mux16_1_out_34), .out_35(mux16_1_out_35),
    .out_36(mux16_1_out_36), .out_37(mux16_1_out_37), .out_38(mux16_1_out_38), .out_39(mux16_1_out_39),
    .out_40(mux16_1_out_40), .out_41(mux16_1_out_41), .out_42(mux16_1_out_42), .out_43(mux16_1_out_43),
    .out_44(mux16_1_out_44), .out_45(mux16_1_out_45), .out_46(mux16_1_out_46), .out_47(mux16_1_out_47),
    .out_48(mux16_1_out_48), .out_49(mux16_1_out_49), .in_1(in_2));
  Mux16 mux16_2 (
    .in_2(in_23), .in_3(in_24), .in_4(in_25), .in_5(in_26), .in_6(in_27), .in_7(in_28), .in_8(in_29),
    .in_9(in_30), .in_10(in_31), .in_11(in_32), .in_12(in_33), .in_13(in_34), .in_14(in_35), .in_15(in_36),
    .in_16(in_37), .in_17(in_38), .in_18(1'b0), .in_19(1'b0), .in_20(1'b0), .in_21(1'b0), .in_22(1'b0),
    .in_23(1'b0), .in_24(1'b0), .in_25(1'b0), .in_26(1'b0), .in_27(1'b0), .in_28(1'b0), .in_29(1'b0),
    .in_30(1'b0), .in_31(1'b0), .in_32(1'b0), .in_33(1'b0), .out_34(mux16_2_out_34), .out_35(mux16_2_out_35),
    .out_36(mux16_2_out_36), .out_37(mux16_2_out_37), .out_38(mux16_2_out_38), .out_39(mux16_2_out_39),
    .out_40(mux16_2_out_40), .out_41(mux16_2_out_41), .out_42(mux16_2_out_42), .out_43(mux16_2_out_43),
    .out_44(mux16_2_out_44), .out_45(mux16_2_out_45), .out_46(mux16_2_out_46), .out_47(mux16_2_out_47),
    .out_48(mux16_2_out_48), .out_49(mux16_2_out_49), .in_1(in_22));
  Not16 not16_1 (
    .in_1(mux16_1_out_34), .in_2(mux16_1_out_35), .in_3(mux16_1_out_36), .in_4(mux16_1_out_37),
    .in_5(mux16_1_out_38), .in_6(mux16_1_out_39), .in_7(mux16_1_out_40), .in_8(mux16_1_out_41),
    .in_9(mux16_1_out_42), .in_10(mux16_1_out_43), .in_11(mux16_1_out_44), .in_12(mux16_1_out_45),
    .in_13(mux16_1_out_46), .in_14(mux16_1_out_47), .in_15(mux16_1_out_48), .in_16(mux16_1_out_49),
    .out_17(not16_1_out_17), .out_18(not16_1_out_18), .out_19(not16_1_out_19), .out_20(not16_1_out_20),
    .out_21(not16_1_out_21), .out_22(not16_1_out_22), .out_23(not16_1_out_23), .out_24(not16_1_out_24),
    .out_25(not16_1_out_25), .out_26(not16_1_out_26), .out_27(not16_1_out_27), .out_28(not16_1_out_28),
    .out_29(not16_1_out_29), .out_30(not16_1_out_30), .out_31(not16_1_out_31), .out_32(not16_1_out_32));
  Not16 not16_2 (
    .in_1(mux16_2_out_34), .in_2(mux16_2_out_35), .in_3(mux16_2_out_36), .in_4(mux16_2_out_37),
    .in_5(mux16_2_out_38), .in_6(mux16_2_out_39), .in_7(mux16_2_out_40), .in_8(mux16_2_out_41),
    .in_9(mux16_2_out_42), .in_10(mux16_2_out_43), .in_11(mux16_2_out_44), .in_12(mux16_2_out_45),
    .in_13(mux16_2_out_46), .in_14(mux16_2_out_47), .in_15(mux16_2_out_48), .in_16(mux16_2_out_49),
    .out_17(not16_2_out_17), .out_18(not16_2_out_18), .out_19(not16_2_out_19), .out_20(not16_2_out_20),
    .out_21(not16_2_out_21), .out_22(not16_2_out_22), .out_23(not16_2_out_23), .out_24(not16_2_out_24),
    .out_25(not16_2_out_25), .out_26(not16_2_out_26), .out_27(not16_2_out_27), .out_28(not16_2_out_28),
    .out_29(not16_2_out_29), .out_30(not16_2_out_30), .out_31(not16_2_out_31), .out_32(not16_2_out_32));
  Mux16 mux16_3 (
    .in_2(mux16_1_out_34), .in_3(mux16_1_out_35), .in_4(mux16_1_out_36), .in_5(mux16_1_out_37),
    .in_6(mux16_1_out_38), .in_7(mux16_1_out_39), .in_8(mux16_1_out_40), .in_9(mux16_1_out_41),
    .in_10(mux16_1_out_42), .in_11(mux16_1_out_43), .in_12(mux16_1_out_44), .in_13(mux16_1_out_45),
    .in_14(mux16_1_out_46), .in_15(mux16_1_out_47), .in_16(mux16_1_out_48), .in_17(mux16_1_out_49),
    .in_18(not16_1_out_17), .in_19(not16_1_out_18), .in_20(not16_1_out_19), .in_21(not16_1_out_20),
    .in_22(not16_1_out_21), .in_23(not16_1_out_22), .in_24(not16_1_out_23), .in_25(not16_1_out_24),
    .in_26(not16_1_out_25), .in_27(not16_1_out_26), .in_28(not16_1_out_27), .in_29(not16_1_out_28),
    .in_30(not16_1_out_29), .in_31(not16_1_out_30), .in_32(not16_1_out_31), .in_33(not16_1_out_32),
    .out_34(mux16_3_out_34), .out_35(mux16_3_out_35), .out_36(mux16_3_out_36), .out_37(mux16_3_out_37),
    .out_38(mux16_3_out_38), .out_39(mux16_3_out_39), .out_40(mux16_3_out_40), .out_41(mux16_3_out_41),
    .out_42(mux16_3_out_42), .out_43(mux16_3_out_43), .out_44(mux16_3_out_44), .out_45(mux16_3_out_45),
    .out_46(mux16_3_out_46), .out_47(mux16_3_out_47), .out_48(mux16_3_out_48), .out_49(mux16_3_out_49),
    .in_1(in_1));
  Mux16 mux16_4 (
    .in_2(mux16_2_out_34), .in_3(mux16_2_out_35), .in_4(mux16_2_out_36), .in_5(mux16_2_out_37),
    .in_6(mux16_2_out_38), .in_7(mux16_2_out_39), .in_8(mux16_2_out_40), .in_9(mux16_2_out_41),
    .in_10(mux16_2_out_42), .in_11(mux16_2_out_43), .in_12(mux16_2_out_44), .in_13(mux16_2_out_45),
    .in_14(mux16_2_out_46), .in_15(mux16_2_out_47), .in_16(mux16_2_out_48), .in_17(mux16_2_out_49),
    .in_18(not16_2_out_17), .in_19(not16_2_out_18), .in_20(not16_2_out_19), .in_21(not16_2_out_20),
    .in_22(not16_2_out_21), .in_23(not16_2_out_22), .in_24(not16_2_out_23), .in_25(not16_2_out_24),
    .in_26(not16_2_out_25), .in_27(not16_2_out_26), .in_28(not16_2_out_27), .in_29(not16_2_out_28),
    .in_30(not16_2_out_29), .in_31(not16_2_out_30), .in_32(not16_2_out_31), .in_33(not16_2_out_32),
    .out_34(mux16_4_out_34), .out_35(mux16_4_out_35), .out_36(mux16_4_out_36), .out_37(mux16_4_out_37),
    .out_38(mux16_4_out_38), .out_39(mux16_4_out_39), .out_40(mux16_4_out_40), .out_41(mux16_4_out_41),
    .out_42(mux16_4_out_42), .out_43(mux16_4_out_43), .out_44(mux16_4_out_44), .out_45(mux16_4_out_45),
    .out_46(mux16_4_out_46), .out_47(mux16_4_out_47), .out_48(mux16_4_out_48), .out_49(mux16_4_out_49),
    .in_1(in_21));
  AND16 and16_1 (
    .in_1(mux16_3_out_34), .in_2(mux16_3_out_35), .in_3(mux16_3_out_36), .in_4(mux16_3_out_37),
    .in_5(mux16_3_out_38), .in_6(mux16_3_out_39), .in_7(mux16_3_out_40), .in_8(mux16_3_out_41),
    .in_9(mux16_3_out_42), .in_10(mux16_3_out_43), .in_11(mux16_3_out_44), .in_12(mux16_3_out_45),
    .in_13(mux16_3_out_46), .in_14(mux16_3_out_47), .in_15(mux16_3_out_48), .in_16(mux16_3_out_49),
    .in_17(mux16_4_out_34), .in_18(mux16_4_out_35), .in_19(mux16_4_out_36), .in_20(mux16_4_out_37),
    .in_21(mux16_4_out_38), .in_22(mux16_4_out_39), .in_23(mux16_4_out_40), .in_24(mux16_4_out_41),
    .in_25(mux16_4_out_42), .in_26(mux16_4_out_43), .in_27(mux16_4_out_44), .in_28(mux16_4_out_45),
    .in_29(mux16_4_out_46), .in_30(mux16_4_out_47), .in_31(mux16_4_out_48), .in_32(mux16_4_out_49),
    .out_33(and16_1_out_33), .out_34(and16_1_out_34), .out_35(and16_1_out_35), .out_36(and16_1_out_36),
    .out_37(and16_1_out_37), .out_38(and16_1_out_38), .out_39(and16_1_out_39), .out_40(and16_1_out_40),
    .out_41(and16_1_out_41), .out_42(and16_1_out_42), .out_43(and16_1_out_43), .out_44(and16_1_out_44),
    .out_45(and16_1_out_45), .out_46(and16_1_out_46), .out_47(and16_1_out_47), .out_48(and16_1_out_48));
  ADD16 add16_1 (
    .in_2(mux16_3_out_34), .in_3(mux16_4_out_34), .in_4(mux16_3_out_35), .in_5(mux16_4_out_35),
    .in_6(mux16_3_out_36), .in_7(mux16_4_out_36), .in_8(mux16_3_out_37), .in_9(mux16_4_out_37),
    .in_10(mux16_3_out_38), .in_11(mux16_4_out_38), .in_12(mux16_3_out_39), .in_13(mux16_4_out_39),
    .in_14(mux16_3_out_40), .in_15(mux16_4_out_40), .in_16(mux16_3_out_41), .in_17(mux16_4_out_41),
    .in_18(mux16_3_out_42), .in_19(mux16_4_out_42), .in_20(mux16_3_out_43), .in_21(mux16_4_out_43),
    .in_22(mux16_3_out_44), .in_23(mux16_4_out_44), .in_24(mux16_3_out_45), .in_25(mux16_4_out_45),
    .in_26(mux16_3_out_46), .in_27(mux16_4_out_46), .in_28(mux16_3_out_47), .in_29(mux16_4_out_47),
    .in_30(mux16_3_out_48), .in_31(mux16_4_out_48), .in_32(mux16_3_out_49), .in_33(mux16_4_out_49),
    .out_34(add16_1_out_34), .out_35(add16_1_out_35), .out_36(add16_1_out_36), .out_37(add16_1_out_37),
    .out_38(add16_1_out_38), .out_39(add16_1_out_39), .out_40(add16_1_out_40), .out_41(add16_1_out_41),
    .out_42(add16_1_out_42), .out_43(add16_1_out_43), .out_44(add16_1_out_44), .out_45(add16_1_out_45),
    .out_46(add16_1_out_46), .out_47(add16_1_out_47), .out_48(add16_1_out_48), .out_49(add16_1_out_49),
    .in_1(1'b0));
  Mux16 mux16_5 (
    .in_2(and16_1_out_33), .in_3(and16_1_out_34), .in_4(and16_1_out_35), .in_5(and16_1_out_36),
    .in_6(and16_1_out_37), .in_7(and16_1_out_38), .in_8(and16_1_out_39), .in_9(and16_1_out_40),
    .in_10(and16_1_out_41), .in_11(and16_1_out_42), .in_12(and16_1_out_43), .in_13(and16_1_out_44),
    .in_14(and16_1_out_45), .in_15(and16_1_out_46), .in_16(and16_1_out_47), .in_17(and16_1_out_48),
    .in_18(add16_1_out_34), .in_19(add16_1_out_35), .in_20(add16_1_out_36), .in_21(add16_1_out_37),
    .in_22(add16_1_out_38), .in_23(add16_1_out_39), .in_24(add16_1_out_40), .in_25(add16_1_out_41),
    .in_26(add16_1_out_42), .in_27(add16_1_out_43), .in_28(add16_1_out_44), .in_29(add16_1_out_45),
    .in_30(add16_1_out_46), .in_31(add16_1_out_47), .in_32(add16_1_out_48), .in_33(add16_1_out_49),
    .out_34(mux16_5_out_34), .out_35(mux16_5_out_35), .out_36(mux16_5_out_36), .out_37(mux16_5_out_37),
    .out_38(mux16_5_out_38), .out_39(mux16_5_out_39), .out_40(mux16_5_out_40), .out_41(mux16_5_out_41),
    .out_42(mux16_5_out_42), .out_43(mux16_5_out_43), .out_44(mux16_5_out_44), .out_45(mux16_5_out_45),
    .out_46(mux16_5_out_46), .out_47(mux16_5_out_47), .out_48(mux16_5_out_48), .out_49(mux16_5_out_49),
    .in_1(in_20));
  Not16 not16_3 (
    .in_1(mux16_5_out_34), .in_2(mux16_5_out_35), .in_3(mux16_5_out_36), .in_4(mux16_5_out_37),
    .in_5(mux16_5_out_38), .in_6(mux16_5_out_39), .in_7(mux16_5_out_40), .in_8(mux16_5_out_41),
    .in_9(mux16_5_out_42), .in_10(mux16_5_out_43), .in_11(mux16_5_out_44), .in_12(mux16_5_out_45),
    .in_13(mux16_5_out_46), .in_14(mux16_5_out_47), .in_15(mux16_5_out_48), .in_16(mux16_5_out_49),
    .out_17(not16_3_out_17), .out_18(not16_3_out_18), .out_19(not16_3_out_19), .out_20(not16_3_out_20),
    .out_21(not16_3_out_21), .out_22(not16_3_out_22), .out_23(not16_3_out_23), .out_24(not16_3_out_24),
    .out_25(not16_3_out_25), .out_26(not16_3_out_26), .out_27(not16_3_out_27), .out_28(not16_3_out_28),
    .out_29(not16_3_out_29), .out_30(not16_3_out_30), .out_31(not16_3_out_31), .out_32(not16_3_out_32));
  Mux16 mux16_6 (
    .in_2(mux16_5_out_34), .in_3(mux16_5_out_35), .in_4(mux16_5_out_36), .in_5(mux16_5_out_37),
    .in_6(mux16_5_out_38), .in_7(mux16_5_out_39), .in_8(mux16_5_out_40), .in_9(mux16_5_out_41),
    .in_10(mux16_5_out_42), .in_11(mux16_5_out_43), .in_12(mux16_5_out_44), .in_13(mux16_5_out_45),
    .in_14(mux16_5_out_46), .in_15(mux16_5_out_47), .in_16(mux16_5_out_48), .in_17(mux16_5_out_49),
    .in_18(not16_3_out_17), .in_19(not16_3_out_18), .in_20(not16_3_out_19), .in_21(not16_3_out_20),
    .in_22(not16_3_out_21), .in_23(not16_3_out_22), .in_24(not16_3_out_23), .in_25(not16_3_out_24),
    .in_26(not16_3_out_25), .in_27(not16_3_out_26), .in_28(not16_3_out_27), .in_29(not16_3_out_28),
    .in_30(not16_3_out_29), .in_31(not16_3_out_30), .in_32(not16_3_out_31), .in_33(not16_3_out_32),
    .out_34(out_39), .out_35(out_40), .out_36(out_41), .out_37(out_42), .out_38(out_43), .out_39(out_44),
    .out_40(out_45), .out_41(out_46), .out_42(out_47), .out_43(out_48), .out_44(out_49), .out_45(out_50),
    .out_46(out_51), .out_47(out_52), .out_48(out_53), .out_49(out_54), .in_1(in_14));
  Or8Way or8way_1 (
    .in_1(out_39), .in_2(out_40), .in_3(out_41), .in_4(out_42), .in_5(out_43), .in_6(out_44), .in_7(out_45),
    .in_8(out_46), .out_9(or8way_1_out_9));
  Or8Way or8way_2 (
    .in_1(out_47), .in_2(out_48), .in_3(out_49), .in_4(out_50), .in_5(out_51), .in_6(out_52), .in_7(out_53),
    .in_8(out_54), .out_9(or8way_2_out_9));
  OR or_1 (.in_1(or8way_1_out_9), .in_2(or8way_2_out_9), .out_3(or_1_out_3));
  Not not_1 (.in_1(or_1_out_3), .out_2(out_56));

  assign out_55 = out_54;
endmodule

module DFF (
  input  in_1,
  input  in_2,
  output out_3
);

  wire and_1_out_3, and_2_out_3, and_3_out_3, and_4_out_3, nor_1_out_3, nor_2_out_3, nor_4_out_3,
       not_1_out_2, not_2_out_2;

  Not not_1 (.in_1(in_2), .out_2(not_1_out_2));
  Not not_2 (.in_1(in_1), .out_2(not_2_out_2));
  AND and_1 (.in_1(in_1), .in_2(not_1_out_2), .out_3(and_1_out_3));
  AND and_2 (.in_1(not_1_out_2), .in_2(not_2_out_2), .out_3(and_2_out_3));
  NOR nor_1 (.in_1(and_1_out_3), .in_2(nor_2_out_3), .out_3(nor_1_out_3));
  NOR nor_2 (.in_1(nor_1_out_3), .in_2(and_2_out_3), .out_3(nor_2_out_3));
  AND and_3 (.in_1(nor_1_out_3), .in_2(in_2), .out_3(and_3_out_3));
  AND and_4 (.in_1(in_2), .in_2(nor_2_out_3), .out_3(and_4_out_3));
  NOR nor_3 (.in_1(and_3_out_3), .in_2(nor_4_out_3), .out_3(out_3));
  NOR nor_4 (.in_1(out_3), .in_2(and_4_out_3), .out_3(nor_4_out_3));
endmodule

module Bit (
  input  in_1,
  input  in_2,
  input  in_3,
  output out_4
);

  wire mux_1_out_4;

  Mux mux_1 (.in_2(out_4), .in_3(in_2), .out_4(mux_1_out_4), .in_1(in_1));
  DFF dff_1 (.in_1(mux_1_out_4), .out_3(out_4), .in_2(in_3));
endmodule

module Register (
  input  in_1,
  input  in_2,
  input  in_3,
  input  in_4,
  input  in_5,
  input  in_6,
  input  in_7,
  input  in_8,
  input  in_9,
  input  in_10,
  input  in_11,
  input  in_12,
  input  in_13,
  input  in_14,
  input  in_15,
  input  in_16,
  input  in_17,
  input  in_18,
  output out_19,
  output out_20,
  output out_21,
  output out_22,
  output out_23,
  output out_24,
  output out_25,
  output out_26,
  output out_27,
  output out_28,
  output out_29,
  output out_30,
  output out_31,
  output out_32,
  output out_33,
  output out_34
);

  Bit bit_1 (.out_4(out_19), .in_1(in_1), .in_2(in_2), .in_3(in_18));
  Bit bit_2 (.out_4(out_20), .in_1(in_1), .in_2(in_3), .in_3(in_18));
  Bit bit_3 (.out_4(out_21), .in_1(in_1), .in_2(in_4), .in_3(in_18));
  Bit bit_4 (.out_4(out_22), .in_1(in_1), .in_2(in_5), .in_3(in_18));
  Bit bit_5 (.out_4(out_23), .in_1(in_1), .in_2(in_6), .in_3(in_18));
  Bit bit_6 (.out_4(out_24), .in_1(in_1), .in_2(in_7), .in_3(in_18));
  Bit bit_7 (.out_4(out_25), .in_1(in_1), .in_2(in_8), .in_3(in_18));
  Bit bit_8 (.out_4(out_26), .in_1(in_1), .in_2(in_9), .in_3(in_18));
  Bit bit_9 (.out_4(out_27), .in_1(in_1), .in_2(in_10), .in_3(in_18));
  Bit bit_10 (.out_4(out_28), .in_1(in_1), .in_2(in_11), .in_3(in_18));
  Bit bit_11 (.out_4(out_29), .in_1(in_1), .in_2(in_12), .in_3(in_18));
  Bit bit_12 (.out_4(out_30), .in_1(in_1), .in_2(in_13), .in_3(in_18));
  Bit bit_13 (.out_4(out_31), .in_1(in_1), .in_2(in_14), .in_3(in_18));
  Bit bit_14 (.out_4(out_32), .in_1(in_1), .in_2(in_15), .in_3(in_18));
  Bit bit_15 (.out_4(out_33), .in_1(in_1), .in_2(in_16), .in_3(in_18));
  Bit bit_16 (.out_4(out_34), .in_1(in_1), .in_2(in_17), .in_3(in_18));
endmodule

module RAM8 (
  input  in_1,
  input  in_2,
  input  in_3,
  input  in_4,
  input  in_5,
  input  in_6,
  input  in_7,
  input  in_8,
  input  in_9,
  input  in_10,
  input  in_11,
  input  in_12,
  input  in_13,
  input  in_14,
  input  in_15,
  input  in_16,
  input  in_17,
  input  in_18,
  input  in_19,
  input  in_20,
  output out_21,
  output out_22,
  output out_23,
  output out_24,
  output out_25,
  output out_26,
  output out_27,
  output out_28,
  output out_29,
  output out_30,
  output out_31,
  output out_32,
  output out_33,
  output out_34,
  output out_35,
  output out_36
);

  wire clock_1_out, dmux8way_1_out_5, dmux8way_1_out_6, dmux8way_1_out_7, dmux8way_1_out_8, dmux8way_1_out_9,
       dmux8way_1_out_10, dmux8way_1_out_11, dmux8way_1_out_12, register_1_out_19, register_1_out_20,
       register_1_out_21, register_1_out_22, register_1_out_23, register_1_out_24, register_1_out_25,
       register_1_out_26, register_1_out_27, register_1_out_28, register_1_out_29, register_1_out_30,
       register_1_out_31, register_1_out_32, register_1_out_33, register_1_out_34, register_2_out_19,
       register_2_out_20, register_2_out_21, register_2_out_22, register_2_out_23, register_2_out_24,
       register_2_out_25, register_2_out_26, register_2_out_27, register_2_out_28, register_2_out_29,
       register_2_out_30, register_2_out_31, register_2_out_32, register_2_out_33, register_2_out_34,
       register_3_out_19, register_3_out_20, register_3_out_21, register_3_out_22, register_3_out_23,
       register_3_out_24, register_3_out_25, register_3_out_26, register_3_out_27, register_3_out_28,
       register_3_out_29, register_3_out_30, register_3_out_31, register_3_out_32, register_3_out_33,
       register_3_out_34, register_4_out_19, register_4_out_20, register_4_out_21, register_4_out_22,
       register_4_out_23, register_4_out_24, register_4_out_25, register_4_out_26, register_4_out_27,
       register_4_out_28, register_4_out_29, register_4_out_30, register_4_out_31, register_4_out_32,
       register_4_out_33, register_4_out_34, register_5_out_19, register_5_out_20, register_5_out_21,
       register_5_out_22, register_5_out_23, register_5_out_24, register_5_out_25, register_5_out_26,
       register_5_out_27, register_5_out_28, register_5_out_29, register_5_out_30, register_5_out_31,
       register_5_out_32, register_5_out_33, register_5_out_34, register_6_out_19, register_6_out_20,
       register_6_out_21, register_6_out_22, register_6_out_23, register_6_out_24, register_6_out_25,
       register_6_out_26, register_6_out_27, register_6_out_28, register_6_out_29, register_6_out_30,
       register_6_out_31, register_6_out_32, register_6_out_33, register_6_out_34, register_7_out_19,
       register_7_out_20, register_7_out_21, register_7_out_22, register_7_out_23, register_7_out_24,
       register_7_out_25, register_7_out_26, register_7_out_27, register_7_out_28, register_7_out_29,
       register_7_out_30, register_7_out_31, register_7_out_32, register_7_out_33, register_7_out_34,
       register_8_out_19, register_8_out_20, register_8_out_21, register_8_out_22, register_8_out_23,
       register_8_out_24, register_8_out_25, register_8_out_26, register_8_out_27, register_8_out_28,
       register_8_out_29, register_8_out_30, register_8_out_31, register_8_out_32, register_8_out_33,
       register_8_out_34;

  Clock clock_1 (.out(clock_1_out));
  Register register_1 (
    .in_2(in_1), .in_3(in_2), .in_4(in_3), .in_5(in_4), .in_6(in_5), .in_7(in_6), .in_8(in_7), .in_9(in_8),
    .in_10(in_9), .in_11(in_10), .in_12(in_11), .in_13(in_12), .in_14(in_13), .in_15(in_14), .in_16(in_15),
    .in_17(in_16), .out_19(register_1_out_19), .out_20(register_1_out_20), .out_21(register_1_out_21),
    .out_22(register_1_out_22), .out_23(register_1_out_23), .out_24(register_1_out_24),
    .out_25(register_1_out_25), .out_26(register_1_out_26), .out_27(register_1_out_27),
    .out_28(register_1_out_28), .out_29(register_1_out_29), .out_30(register_1_out_30),
    .out_31(register_1_out_31), .out_32(register_1_out_32), .out_33(register_1_out_33),
    .out_34(register_1_out_34), .in_1(dmux8way_1_out_12), .in_18(clock_1_out));
  Register register_2 (
    .in_2(in_1), .in_3(in_2), .in_4(in_3), .in_5(in_4), .in_6(in_5), .in_7(in_6), .in_8(in_7), .in_9(in_8),
    .in_10(in_9), .in_11(in_10), .in_12(in_11), .in_13(in_12), .in_14(in_13), .in_15(in_14), .in_16(in_15),
    .in_17(in_16), .out_19(register_2_out_19), .out_20(register_2_out_20), .out_21(register_2_out_21),
    .out_22(register_2_out_22), .out_23(register_2_out_23), .out_24(register_2_out_24),
    .out_25(register_2_out_25), .out_26(register_2_out_26), .out_27(register_2_out_27),
    .out_28(register_2_out_28), .out_29(register_2_out_29), .out_30(register_2_out_30),
    .out_31(register_2_out_31), .out_32(register_2_out_32), .out_33(register_2_out_33),
    .out_34(register_2_out_34), .in_1(dmux8way_1_out_11), .in_18(clock_1_out));
  Register register_3 (
    .in_2(in_1), .in_3(in_2), .in_4(in_3), .in_5(in_4), .in_6(in_5), .in_7(in_6), .in_8(in_7), .in_9(in_8),
    .in_10(in_9), .in_11(in_10), .in_12(in_11), .in_13(in_12), .in_14(in_13), .in_15(in_14), .in_16(in_15),
    .in_17(in_16), .out_19(register_3_out_19), .out_20(register_3_out_20), .out_21(register_3_out_21),
    .out_22(register_3_out_22), .out_23(register_3_out_23), .out_24(register_3_out_24),
    .out_25(register_3_out_25), .out_26(register_3_out_26), .out_27(register_3_out_27),
    .out_28(register_3_out_28), .out_29(register_3_out_29), .out_30(register_3_out_30),
    .out_31(register_3_out_31), .out_32(register_3_out_32), .out_33(register_3_out_33),
    .out_34(register_3_out_34), .in_1(dmux8way_1_out_10), .in_18(clock_1_out));
  Mux8Way16 mux8way16_1 (
    .in_4(register_8_out_19), .in_5(register_8_out_20), .in_6(register_8_out_21), .in_7(register_8_out_22),
    .in_8(register_8_out_23), .in_9(register_8_out_24), .in_10(register_8_out_25), .in_11(register_8_out_26),
    .in_12(register_8_out_27), .in_13(register_8_out_28), .in_14(register_8_out_29),
    .in_15(register_8_out_30), .in_16(register_8_out_31), .in_17(register_8_out_32),
    .in_18(register_8_out_33), .in_19(register_8_out_34), .in_20(register_7_out_19),
    .in_21(register_7_out_20), .in_22(register_7_out_21), .in_23(register_7_out_22),
    .in_24(register_7_out_23), .in_25(register_7_out_24), .in_26(register_7_out_25),
    .in_27(register_7_out_26), .in_28(register_7_out_27), .in_29(register_7_out_28),
    .in_30(register_7_out_29), .in_31(register_7_out_30), .in_32(register_7_out_31),
    .in_33(register_7_out_32), .in_34(register_7_out_33), .in_35(register_7_out_34),
    .in_36(register_6_out_19), .in_37(register_6_out_20), .in_38(register_6_out_21),
    .in_39(register_6_out_22), .in_40(register_6_out_23), .in_41(register_6_out_24),
    .in_42(register_6_out_25), .in_43(register_6_out_26), .in_44(register_6_out_27),
    .in_45(register_6_out_28), .in_46(register_6_out_29), .in_47(register_6_out_30),
    .in_48(register_6_out_31), .in_49(register_6_out_32), .in_50(register_6_out_33),
    .in_51(register_6_out_34), .in_52(register_5_out_19), .in_53(register_5_out_20),
    .in_54(register_5_out_21), .in_55(register_5_out_22), .in_56(register_5_out_23),
    .in_57(register_5_out_24), .in_58(register_5_out_25), .in_59(register_5_out_26),
    .in_60(register_5_out_27), .in_61(register_5_out_28), .in_62(register_5_out_29),
    .in_63(register_5_out_30), .in_64(register_5_out_31), .in_65(register_5_out_32),
    .in_66(register_5_out_33), .in_67(register_5_out_34), .in_68(register_4_out_19),
    .in_69(register_4_out_20), .in_70(register_4_out_21), .in_71(register_4_out_22),
    .in_72(register_4_out_23), .in_73(register_4_out_24), .in_74(register_4_out_25),
    .in_75(register_4_out_26), .in_76(register_4_out_27), .in_77(register_4_out_28),
    .in_78(register_4_out_29), .in_79(register_4_out_30), .in_80(register_4_out_31),
    .in_81(register_4_out_32), .in_82(register_4_out_33), .in_83(register_4_out_34),
    .in_84(register_3_out_19), .in_85(register_3_out_20), .in_86(register_3_out_21),
    .in_87(register_3_out_22), .in_88(register_3_out_23), .in_89(register_3_out_24),
    .in_90(register_3_out_25), .in_91(register_3_out_26), .in_92(register_3_out_27),
    .in_93(register_3_out_28), .in_94(register_3_out_29), .in_95(register_3_out_30),
    .in_96(register_3_out_31), .in_97(register_3_out_32), .in_98(register_3_out_33),
    .in_99(register_3_out_34), .in_100(register_2_out_19), .in_101(register_2_out_20),
    .in_102(register_2_out_21), .in_103(register_2_out_22), .in_104(register_2_out_23),
    .in_105(register_2_out_24), .in_106(register_2_out_25), .in_107(register_2_out_26),
    .in_108(register_2_out_27), .in_109(register_2_out_28), .in_110(register_2_out_29),
    .in_111(register_2_out_30), .in_112(register_2_out_31), .in_113(register_2_out_32),
    .in_114(register_2_out_33), .in_115(register_2_out_34), .in_116(register_1_out_19),
    .in_117(register_1_out_20), .in_118(register_1_out_21), .in_119(register_1_out_22),
    .in_120(register_1_out_23), .in_121(register_1_out_24), .in_122(register_1_out_25),
    .in_123(register_1_out_26), .in_124(register_1_out_27), .in_125(register_1_out_28),
    .in_126(register_1_out_29), .in_127(register_1_out_30), .in_128(register_1_out_31),
    .in_129(register_1_out_32), .in_130(register_1_out_33), .in_131(register_1_out_34), .out_132(out_21),
    .out_133(out_22), .out_134(out_23), .out_135(out_24), .out_136(out_25), .out_137(out_26),
    .out_138(out_27), .out_139(out_28), .out_140(out_29), .out_141(out_30), .out_142(out_31),
    .out_143(out_32), .out_144(out_33), .out_145(out_34), .out_146(out_35), .out_147(out_36), .in_2(in_20),
    .in_3(in_19), .in_1(in_18));
  Register register_4 (
    .in_2(in_1), .in_3(in_2), .in_4(in_3), .in_5(in_4), .in_6(in_5), .in_7(in_6), .in_8(in_7), .in_9(in_8),
    .in_10(in_9), .in_11(in_10), .in_12(in_11), .in_13(in_12), .in_14(in_13), .in_15(in_14), .in_16(in_15),
    .in_17(in_16), .out_19(register_4_out_19), .out_20(register_4_out_20), .out_21(register_4_out_21),
    .out_22(register_4_out_22), .out_23(register_4_out_23), .out_24(register_4_out_24),
    .out_25(register_4_out_25), .out_26(register_4_out_26), .out_27(register_4_out_27),
    .out_28(register_4_out_28), .out_29(register_4_out_29), .out_30(register_4_out_30),
    .out_31(register_4_out_31), .out_32(register_4_out_32), .out_33(register_4_out_33),
    .out_34(register_4_out_34), .in_1(dmux8way_1_out_9), .in_18(clock_1_out));
  Register register_5 (
    .in_2(in_1), .in_3(in_2), .in_4(in_3), .in_5(in_4), .in_6(in_5), .in_7(in_6), .in_8(in_7), .in_9(in_8),
    .in_10(in_9), .in_11(in_10), .in_12(in_11), .in_13(in_12), .in_14(in_13), .in_15(in_14), .in_16(in_15),
    .in_17(in_16), .out_19(register_5_out_19), .out_20(register_5_out_20), .out_21(register_5_out_21),
    .out_22(register_5_out_22), .out_23(register_5_out_23), .out_24(register_5_out_24),
    .out_25(register_5_out_25), .out_26(register_5_out_26), .out_27(register_5_out_27),
    .out_28(register_5_out_28), .out_29(register_5_out_29), .out_30(register_5_out_30),
    .out_31(register_5_out_31), .out_32(register_5_out_32), .out_33(register_5_out_33),
    .out_34(register_5_out_34), .in_1(dmux8way_1_out_8), .in_18(clock_1_out));
  Register register_6 (
    .in_2(in_1), .in_3(in_2), .in_4(in_3), .in_5(in_4), .in_6(in_5), .in_7(in_6), .in_8(in_7), .in_9(in_8),
    .in_10(in_9), .in_11(in_10), .in_12(in_11), .in_13(in_12), .in_14(in_13), .in_15(in_14), .in_16(in_15),
    .in_17(in_16), .out_19(register_6_out_19), .out_20(register_6_out_20), .out_21(register_6_out_21),
    .out_22(register_6_out_22), .out_23(register_6_out_23), .out_24(register_6_out_24),
    .out_25(register_6_out_25), .out_26(register_6_out_26), .out_27(register_6_out_27),
    .out_28(register_6_out_28), .out_29(register_6_out_29), .out_30(register_6_out_30),
    .out_31(register_6_out_31), .out_32(register_6_out_32), .out_33(register_6_out_33),
    .out_34(register_6_out_34), .in_1(dmux8way_1_out_7), .in_18(clock_1_out));
  Register register_7 (
    .in_2(in_1), .in_3(in_2), .in_4(in_3), .in_5(in_4), .in_6(in_5), .in_7(in_6), .in_8(in_7), .in_9(in_8),
    .in_10(in_9), .in_11(in_10), .in_12(in_11), .in_13(in_12), .in_14(in_13), .in_15(in_14), .in_16(in_15),
    .in_17(in_16), .out_19(register_7_out_19), .out_20(register_7_out_20), .out_21(register_7_out_21),
    .out_22(register_7_out_22), .out_23(register_7_out_23), .out_24(register_7_out_24),
    .out_25(register_7_out_25), .out_26(register_7_out_26), .out_27(register_7_out_27),
    .out_28(register_7_out_28), .out_29(register_7_out_29), .out_30(register_7_out_30),
    .out_31(register_7_out_31), .out_32(register_7_out_32), .out_33(register_7_out_33),
    .out_34(register_7_out_34), .in_1(dmux8way_1_out_6), .in_18(clock_1_out));
  Register register_8 (
    .in_2(in_1), .in_3(in_2), .in_4(in_3), .in_5(in_4), .in_6(in_5), .in_7(in_6), .in_8(in_7), .in_9(in_8),
    .in_10(in_9), .in_11(in_10), .in_12(in_11), .in_13(in_12), .in_14(in_13), .in_15(in_14), .in_16(in_15),
    .in_17(in_16), .out_19(register_8_out_19), .out_20(register_8_out_20), .out_21(register_8_out_21),
    .out_22(register_8_out_22), .out_23(register_8_out_23), .out_24(register_8_out_24),
    .out_25(register_8_out_25), .out_26(register_8_out_26), .out_27(register_8_out_27),
    .out_28(register_8_out_28), .out_29(register_8_out_29), .out_30(register_8_out_30),
    .out_31(register_8_out_31), .out_32(register_8_out_32), .out_33(register_8_out_33),
    .out_34(register_8_out_34), .in_1(dmux8way_1_out_5), .in_18(clock_1_out));
  DMux8Way dmux8way_1 (
    .in_4(in_17), .out_5(dmux8way_1_out_5), .out_6(dmux8way_1_out_6), .out_7(dmux8way_1_out_7),
    .out_8(dmux8way_1_out_8), .out_9(dmux8way_1_out_9), .out_10(dmux8way_1_out_10),
    .out_11(dmux8way_1_out_11), .out_12(dmux8way_1_out_12), .in_1(in_18), .in_2(in_19), .in_3(in_20));
endmodule

module RAM64 (
  input  in_1,
  input  in_2,
  input  in_3,
  input  in_4,
  input  in_5,
  input  in_6,
  input  in_7,
  input  in_8,
  input  in_9,
  input  in_10,
  input  in_11,
  input  in_12,
  input  in_13,
  input  in_14,
  input  in_15,
  input  in_16,
  input  in_17,
  input  in_18,
  input  in_19,
  input  in_20,
  input  in_21,
  output out_22,
  output out_23,
  output out_24,
  output out_25,
  output out_26,
  output out_27,
  output out_28,
  output out_29,
  output out_30,
  output out_31,
  output out_32,
  output out_33,
  output out_34,
  output out_35,
  output out_36,
  output out_37
);

  wire dmux8way_1_out_5, dmux8way_1_out_6, dmux8way_1_out_7, dmux8way_1_out_8, dmux8way_1_out_9,
       dmux8way_1_out_10, dmux8way_1_out_11, dmux8way_1_out_12, register_1_out_19, register_1_out_20,
       register_1_out_21, register_1_out_22, register_1_out_23, register_1_out_24, register_1_out_25,
       register_1_out_26, register_1_out_27, register_1_out_28, register_1_out_29, register_1_out_30,
       register_1_out_31, register_1_out_32, register_1_out_33, register_1_out_34, register_2_out_19,
       register_2_out_20, register_2_out_21, register_2_out_22, register_2_out_23, register_2_out_24,
       register_2_out_25, register_2_out_26, register_2_out_27, register_2_out_28, register_2_out_29,
       register_2_out_30, register_2_out_31, register_2_out_32, register_2_out_33, register_2_out_34,
       register_3_out_19, register_3_out_20, register_3_out_21, register_3_out_22, register_3_out_23,
       register_3_out_24, register_3_out_25, register_3_out_26, register_3_out_27, register_3_out_28,
       register_3_out_29, register_3_out_30, register_3_out_31, register_3_out_32, register_3_out_33,
       register_3_out_34, register_4_out_19, register_4_out_20, register_4_out_21, register_4_out_22,
       register_4_out_23, register_4_out_24, register_4_out_25, register_4_out_26, register_4_out_27,
       register_4_out_28, register_4_out_29, register_4_out_30, register_4_out_31, register_4_out_32,
       register_4_out_33, register_4_out_34, register_5_out_19, register_5_out_20, register_5_out_21,
       register_5_out_22, register_5_out_23, register_5_out_24, register_5_out_25, register_5_out_26,
       register_5_out_27, register_5_out_28, register_5_out_29, register_5_out_30, register_5_out_31,
       register_5_out_32, register_5_out_33, register_5_out_34, register_6_out_19, register_6_out_20,
       register_6_out_21, register_6_out_22, register_6_out_23, register_6_out_24, register_6_out_25,
       register_6_out_26, register_6_out_27, register_6_out_28, register_6_out_29, register_6_out_30,
       register_6_out_31, register_6_out_32, register_6_out_33, register_6_out_34, register_7_out_19,
       register_7_out_20, register_7_out_21, register_7_out_22, register_7_out_23, register_7_out_24,
       register_7_out_25, register_7_out_26, register_7_out_27, register_7_out_28, register_7_out_29,
       register_7_out_30, register_7_out_31, register_7_out_32, register_7_out_33, register_7_out_34,
       register_8_out_19, register_8_out_20, register_8_out_21, register_8_out_22, register_8_out_23,
       register_8_out_24, register_8_out_25, register_8_out_26, register_8_out_27, register_8_out_28,
       register_8_out_29, register_8_out_30, register_8_out_31, register_8_out_32, register_8_out_33,
       register_8_out_34;

  RAM8 ram8_1 ();  // open: in_1, in_2, in_3, in_4, in_5, in_6, in_7, in_8, in_9, in_10, in_11, in_12, in_13, in_14, in_15, in_16, out_21, out_22, out_23, out_24, out_25, out_26, out_27, out_28, out_29, out_30, out_31, out_32, out_33, out_34, out_35, out_36, in_17, in_18, in_19, in_20
  Register register_1 (
    .in_2(in_1), .in_3(in_2), .in_4(in_3), .in_5(in_4), .in_6(in_5), .in_7(in_6), .in_8(in_7), .in_9(in_8),
    .in_10(in_9), .in_11(in_10), .in_12(in_11), .in_13(in_12), .in_14(in_13), .in_15(in_14), .in_16(in_15),
    .in_17(in_16), .out_19(register_1_out_19), .out_20(register_1_out_20), .out_21(register_1_out_21),
    .out_22(register_1_out_22), .out_23(register_1_out_23), .out_24(register_1_out_24),
    .out_25(register_1_out_25), .out_26(register_1_out_26), .out_27(register_1_out_27),
    .out_28(register_1_out_28), .out_29(register_1_out_29), .out_30(register_1_out_30),
    .out_31(register_1_out_31), .out_32(register_1_out_32), .out_33(register_1_out_33),
    .out_34(register_1_out_34), .in_1(dmux8way_1_out_12), .in_18(in_21));
  Register register_2 (
    .in_2(in_1), .in_3(in_2), .in_4(in_3), .in_5(in_4), .in_6(in_5), .in_7(in_6), .in_8(in_7), .in_9(in_8),
    .in_10(in_9), .in_11(in_10), .in_12(in_11), .in_13(in_12), .in_14(in_13), .in_15(in_14), .in_16(in_15),
    .in_17(in_16), .out_19(register_2_out_19), .out_20(register_2_out_20), .out_21(register_2_out_21),
    .out_22(register_2_out_22), .out_23(register_2_out_23), .out_24(register_2_out_24),
    .out_25(register_2_out_25), .out_26(register_2_out_26), .out_27(register_2_out_27),
    .out_28(register_2_out_28), .out_29(register_2_out_29), .out_30(register_2_out_30),
    .out_31(register_2_out_31), .out_32(register_2_out_32), .out_33(register_2_out_33),
    .out_34(register_2_out_34), .in_1(dmux8way_1_out_11), .in_18(in_21));
  Register register_3 (
    .in_2(in_1), .in_3(in_2), .in_4(in_3), .in_5(in_4), .in_6(in_5), .in_7(in_6), .in_8(in_7), .in_9(in_8),
    .in_10(in_9), .in_11(in_10), .in_12(in_11), .in_13(in_12), .in_14(in_13), .in_15(in_14), .in_16(in_15),
    .in_17(in_16), .out_19(register_3_out_19), .out_20(register_3_out_20), .out_21(register_3_out_21),
    .out_22(register_3_out_22), .out_23(register_3_out_23), .out_24(register_3_out_24),
    .out_25(register_3_out_25), .out_26(register_3_out_26), .out_27(register_3_out_27),
    .out_28(register_3_out_28), .out_29(register_3_out_29), .out_30(register_3_out_30),
    .out_31(register_3_out_31), .out_32(register_3_out_32), .out_33(register_3_out_33),
    .out_34(register_3_out_34), .in_1(dmux8way_1_out_10), .in_18(in_21));
  Mux8Way16 mux8way16_1 (
    .in_4(register_8_out_19), .in_5(register_8_out_20), .in_6(register_8_out_21), .in_7(register_8_out_22),
    .in_8(register_8_out_23), .in_9(register_8_out_24), .in_10(register_8_out_25), .in_11(register_8_out_26),
    .in_12(register_8_out_27), .in_13(register_8_out_28), .in_14(register_8_out_29),
    .in_15(register_8_out_30), .in_16(register_8_out_31), .in_17(register_8_out_32),
    .in_18(register_8_out_33), .in_19(register_8_out_34), .in_20(register_7_out_19),
    .in_21(register_7_out_20), .in_22(register_7_out_21), .in_23(register_7_out_22),
    .in_24(register_7_out_23), .in_25(register_7_out_24), .in_26(register_7_out_25),
    .in_27(register_7_out_26), .in_28(register_7_out_27), .in_29(register_7_out_28),
    .in_30(register_7_out_29), .in_31(register_7_out_30), .in_32(register_7_out_31),
    .in_33(register_7_out_32), .in_34(register_7_out_33), .in_35(register_7_out_34),
    .in_36(register_6_out_19), .in_37(register_6_out_20), .in_38(register_6_out_21),
    .in_39(register_6_out_22), .in_40(register_6_out_23), .in_41(register_6_out_24),
    .in_42(register_6_out_25), .in_43(register_6_out_26), .in_44(register_6_out_27),
    .in_45(register_6_out_28), .in_46(register_6_out_29), .in_47(register_6_out_30),
    .in_48(register_6_out_31), .in_49(register_6_out_32), .in_50(register_6_out_33),
    .in_51(register_6_out_34), .in_52(register_5_out_19), .in_53(register_5_out_20),
    .in_54(register_5_out_21), .in_55(register_5_out_22), .in_56(register_5_out_23),
    .in_57(register_5_out_24), .in_58(register_5_out_25), .in_59(register_5_out_26),
    .in_60(register_5_out_27), .in_61(register_5_out_28), .in_62(register_5_out_29),
    .in_63(register_5_out_30), .in_64(register_5_out_31), .in_65(register_5_out_32),
    .in_66(register_5_out_33), .in_67(register_5_out_34), .in_68(register_4_out_19),
    .in_69(register_4_out_20), .in_70(register_4_out_21), .in_71(register_4_out_22),
    .in_72(register_4_out_23), .in_73(register_4_out_24), .in_74(register_4_out_25),
    .in_75(register_4_out_26), .in_76(register_4_out_27), .in_77(register_4_out_28),
    .in_78(register_4_out_29), .in_79(register_4_out_30), .in_80(register_4_out_31),
    .in_81(register_4_out_32), .in_82(register_4_out_33), .in_83(register_4_out_34),
    .in_84(register_3_out_19), .in_85(register_3_out_20), .in_86(register_3_out_21),
    .in_87(register_3_out_22), .in_88(register_3_out_23), .in_89(register_3_out_24),
    .in_90(register_3_out_25), .in_91(register_3_out_26), .in_92(register_3_out_27),
    .in_93(register_3_out_28), .in_94(register_3_out_29), .in_95(register_3_out_30),
    .in_96(register_3_out_31), .in_97(register_3_out_32), .in_98(register_3_out_33),
    .in_99(register_3_out_34), .in_100(register_2_out_19), .in_101(register_2_out_20),
    .in_102(register_2_out_21), .in_103(register_2_out_22), .in_104(register_2_out_23),
    .in_105(register_2_out_24), .in_106(register_2_out_25), .in_107(register_2_out_26),
    .in_108(register_2_out_27), .in_109(register_2_out_28), .in_110(register_2_out_29),
    .in_111(register_2_out_30), .in_112(register_2_out_31), .in_113(register_2_out_32),
    .in_114(register_2_out_33), .in_115(register_2_out_34), .in_116(register_1_out_19),
    .in_117(register_1_out_20), .in_118(register_1_out_21), .in_119(register_1_out_22),
    .in_120(register_1_out_23), .in_121(register_1_out_24), .in_122(register_1_out_25),
    .in_123(register_1_out_26), .in_124(register_1_out_27), .in_125(register_1_out_28),
    .in_126(register_1_out_29), .in_127(register_1_out_30), .in_128(register_1_out_31),
    .in_129(register_1_out_32), .in_130(register_1_out_33), .in_131(register_1_out_34), .out_132(out_22),
    .out_133(out_23), .out_134(out_24), .out_135(out_25), .out_136(out_26), .out_137(out_27),
    .out_138(out_28), .out_139(out_29), .out_140(out_30), .out_141(out_31), .out_142(out_32),
    .out_143(out_33), .out_144(out_34), .out_145(out_35), .out_146(out_36), .out_147(out_37), .in_2(in_20),
    .in_3(in_19), .in_1(in_18));
  Register register_4 (
    .in_2(in_1), .in_3(in_2), .in_4(in_3), .in_5(in_4), .in_6(in_5), .in_7(in_6), .in_8(in_7), .in_9(in_8),
    .in_10(in_9), .in_11(in_10), .in_12(in_11), .in_13(in_12), .in_14(in_13), .in_15(in_14), .in_16(in_15),
    .in_17(in_16), .out_19(register_4_out_19), .out_20(register_4_out_20), .out_21(register_4_out_21),
    .out_22(register_4_out_22), .out_23(register_4_out_23), .out_24(register_4_out_24),
    .out_25(register_4_out_25), .out_26(register_4_out_26), .out_27(register_4_out_27),
    .out_28(register_4_out_28), .out_29(register_4_out_29), .out_30(register_4_out_30),
    .out_31(register_4_out_31), .out_32(register_4_out_32), .out_33(register_4_out_33),
    .out_34(register_4_out_34), .in_1(dmux8way_1_out_9), .in_18(in_21));
  Register register_5 (
    .in_2(in_1), .in_3(in_2), .in_4(in_3), .in_5(in_4), .in_6(in_5), .in_7(in_6), .in_8(in_7), .in_9(in_8),
    .in_10(in_9), .in_11(in_10), .in_12(in_11), .in_13(in_12), .in_14(in_13), .in_15(in_14), .in_16(in_15),
    .in_17(in_16), .out_19(register_5_out_19), .out_20(register_5_out_20), .out_21(register_5_out_21),
    .out_22(register_5_out_22), .out_23(register_5_out_23), .out_24(register_5_out_24),
    .out_25(register_5_out_25), .out_26(register_5_out_26), .out_27(register_5_out_27),
    .out_28(register_5_out_28), .out_29(register_5_out_29), .out_30(register_5_out_30),
    .out_31(register_5_out_31), .out_32(register_5_out_32), .out_33(register_5_out_33),
    .out_34(register_5_out_34), .in_1(dmux8way_1_out_8), .in_18(in_21));
  Register register_6 (
    .in_2(in_1), .in_3(in_2), .in_4(in_3), .in_5(in_4), .in_6(in_5), .in_7(in_6), .in_8(in_7), .in_9(in_8),
    .in_10(in_9), .in_11(in_10), .in_12(in_11), .in_13(in_12), .in_14(in_13), .in_15(in_14), .in_16(in_15),
    .in_17(in_16), .out_19(register_6_out_19), .out_20(register_6_out_20), .out_21(register_6_out_21),
    .out_22(register_6_out_22), .out_23(register_6_out_23), .out_24(register_6_out_24),
    .out_25(register_6_out_25), .out_26(register_6_out_26), .out_27(register_6_out_27),
    .out_28(register_6_out_28), .out_29(register_6_out_29), .out_30(register_6_out_30),
    .out_31(register_6_out_31), .out_32(register_6_out_32), .out_33(register_6_out_33),
    .out_34(register_6_out_34), .in_1(dmux8way_1_out_7), .in_18(in_21));
  Register register_7 (
    .in_2(in_1), .in_3(in_2), .in_4(in_3), .in_5(in_4), .in_6(in_5), .in_7(in_6), .in_8(in_7), .in_9(in_8),
    .in_10(in_9), .in_11(in_10), .in_12(in_11), .in_13(in_12), .in_14(in_13), .in_15(in_14), .in_16(in_15),
    .in_17(in_16), .out_19(register_7_out_19), .out_20(register_7_out_20), .out_21(register_7_out_21),
    .out_22(register_7_out_22), .out_23(register_7_out_23), .out_24(register_7_out_24),
    .out_25(register_7_out_25), .out_26(register_7_out_26), .out_27(register_7_out_27),
    .out_28(register_7_out_28), .out_29(register_7_out_29), .out_30(register_7_out_30),
    .out_31(register_7_out_31), .out_32(register_7_out_32), .out_33(register_7_out_33),
    .out_34(register_7_out_34), .in_1(dmux8way_1_out_6), .in_18(in_21));
  Register register_8 (
    .in_2(in_1), .in_3(in_2), .in_4(in_3), .in_5(in_4), .in_6(in_5), .in_7(in_6), .in_8(in_7), .in_9(in_8),
    .in_10(in_9), .in_11(in_10), .in_12(in_11), .in_13(in_12), .in_14(in_13), .in_15(in_14), .in_16(in_15),
    .in_17(in_16), .out_19(register_8_out_19), .out_20(register_8_out_20), .out_21(register_8_out_21),
    .out_22(register_8_out_22), .out_23(register_8_out_23), .out_24(register_8_out_24),
    .out_25(register_8_out_25), .out_26(register_8_out_26), .out_27(register_8_out_27),
    .out_28(register_8_out_28), .out_29(register_8_out_29), .out_30(register_8_out_30),
    .out_31(register_8_out_31), .out_32(register_8_out_32), .out_33(register_8_out_33),
    .out_34(register_8_out_34), .in_1(dmux8way_1_out_5), .in_18(in_21));
  DMux8Way dmux8way_1 (
    .in_4(in_17), .out_5(dmux8way_1_out_5), .out_6(dmux8way_1_out_6), .out_7(dmux8way_1_out_7),
    .out_8(dmux8way_1_out_8), .out_9(dmux8way_1_out_9), .out_10(dmux8way_1_out_10),
    .out_11(dmux8way_1_out_11), .out_12(dmux8way_1_out_12), .in_1(in_18), .in_2(in_19), .in_3(in_20));
endmodule

module PC (
  input  inc,
  input  load,
  input  in_3,
  input  in_4,
  input  in_5,
  input  in_6,
  input  in_7,
  input  in_8,
  input  in_9,
  input  in_10,
  input  in_11,
  input  in_12,
  input  in_13,
  input  in_14,
  input  in_15,
  input  in_16,
  input  in_17,
  input  in_18,
  input  in_19,
  input  in_20,
  output out_21,
  output out_22,
  output out_23,
  output out_24,
  output out_25,
  output out_26,
  output out_27,
  output out_28,
  output out_29,
  output out_30,
  output out_31,
  output out_32,
  output out_33,
  output out_34,
  output out_35,
  output out_36
);

  wire inc16_1_out_18, inc16_1_out_19, inc16_1_out_20, inc16_1_out_21, inc16_1_out_22, inc16_1_out_23,
       inc16_1_out_24, inc16_1_out_25, inc16_1_out_26, inc16_1_out_27, inc16_1_out_28, inc16_1_out_29,
       inc16_1_out_30, inc16_1_out_31, inc16_1_out_32, inc16_1_out_33, mux16_1_out_34, mux16_1_out_35,
       mux16_1_out_36, mux16_1_out_37, mux16_1_out_38, mux16_1_out_39, mux16_1_out_40, mux16_1_out_41,
       mux16_1_out_42, mux16_1_out_43, mux16_1_out_44, mux16_1_out_45, mux16_1_out_46, mux16_1_out_47,
       mux16_1_out_48, mux16_1_out_49, mux16_2_out_34, mux16_2_out_35, mux16_2_out_36, mux16_2_out_37,
       mux16_2_out_38, mux16_2_out_39, mux16_2_out_40, mux16_2_out_41, mux16_2_out_42, mux16_2_out_43,
       mux16_2_out_44, mux16_2_out_45, mux16_2_out_46, mux16_2_out_47, mux16_2_out_48, mux16_2_out_49,
       mux16_3_out_34, mux16_3_out_35, mux16_3_out_36, mux16_3_out_37, mux16_3_out_38, mux16_3_out_39,
       mux16_3_out_40, mux16_3_out_41, mux16_3_out_42, mux16_3_out_43, mux16_3_out_44, mux16_3_out_45,
       mux16_3_out_46, mux16_3_out_47, mux16_3_out_48, mux16_3_out_49;

  Mux16 mux16_1 (
    .in_2(out_21), .in_3(out_22), .in_4(out_23), .in_5(out_24), .in_6(out_25), .in_7(out_26), .in_8(out_27),
    .in_9(out_28), .in_10(out_29), .in_11(out_30), .in_12(out_31), .in_13(out_32), .in_14(out_33),
    .in_15(out_34), .in_16(out_35), .in_17(out_36), .in_18(inc16_1_out_18), .in_19(inc16_1_out_19),
    .in_20(inc16_1_out_20), .in_21(inc16_1_out_21), .in_22(inc16_1_out_22), .in_23(inc16_1_out_23),
    .in_24(inc16_1_out_24), .in_25(inc16_1_out_25), .in_26(inc16_1_out_26), .in_27(inc16_1_out_27),
    .in_28(inc16_1_out_28), .in_29(inc16_1_out_29), .in_30(inc16_1_out_30), .in_31(inc16_1_out_31),
    .in_32(inc16_1_out_32), .in_33(inc16_1_out_33), .out_34(mux16_1_out_34), .out_35(mux16_1_out_35),
    .out_36(mux16_1_out_36), .out_37(mux16_1_out_37), .out_38(mux16_1_out_38), .out_39(mux16_1_out_39),
    .out_40(mux16_1_out_40), .out_41(mux16_1_out_41), .out_42(mux16_1_out_42), .out_43(mux16_1_out_43),
    .out_44(mux16_1_out_44), .out_45(mux16_1_out_45), .out_46(mux16_1_out_46), .out_47(mux16_1_out_47),
    .out_48(mux16_1_out_48), .out_49(mux16_1_out_49), .in_1(inc));
  Mux16 mux16_2 (
    .in_2(mux16_1_out_34), .in_3(mux16_1_out_35), .in_4(mux16_1_out_36), .in_5(mux16_1_out_37),
    .in_6(mux16_1_out_38), .in_7(mux16_1_out_39), .in_8(mux16_1_out_40), .in_9(mux16_1_out_41),
    .in_10(mux16_1_out_42), .in_11(mux16_1_out_43), .in_12(mux16_1_out_44), .in_13(mux16_1_out_45),
    .in_14(mux16_1_out_46), .in_15(mux16_1_out_47), .in_16(mux16_1_out_48), .in_17(mux16_1_out_49),
    .in_18(in_4), .in_19(in_5), .in_20(in_6), .in_21(in_7), .in_22(in_8), .in_23(in_9), .in_24(in_10),
    .in_25(in_11), .in_26(in_12), .in_27(in_13), .in_28(in_14), .in_29(in_15), .in_30(in_16), .in_31(in_17),
    .in_32(in_18), .in_33(in_19), .out_34(mux16_2_out_34), .out_35(mux16_2_out_35), .out_36(mux16_2_out_36),
    .out_37(mux16_2_out_37), .out_38(mux16_2_out_38), .out_39(mux16_2_out_39), .out_40(mux16_2_out_40),
    .out_41(mux16_2_out_41), .out_42(mux16_2_out_42), .out_43(mux16_2_out_43), .out_44(mux16_2_out_44),
    .out_45(mux16_2_out_45), .out_46(mux16_2_out_46), .out_47(mux16_2_out_47), .out_48(mux16_2_out_48),
    .out_49(mux16_2_out_49), .in_1(load));
  Mux16 mux16_3 (
    .in_2(mux16_2_out_34), .in_3(mux16_2_out_35), .in_4(mux16_2_out_36), .in_5(mux16_2_out_37),
    .in_6(mux16_2_out_38), .in_7(mux16_2_out_39), .in_8(mux16_2_out_40), .in_9(mux16_2_out_41),
    .in_10(mux16_2_out_42), .in_11(mux16_2_out_43), .in_12(mux16_2_out_44), .in_13(mux16_2_out_45),
    .in_14(mux16_2_out_46), .in_15(mux16_2_out_47), .in_16(mux16_2_out_48), .in_17(mux16_2_out_49),
    .in_18(1'b0), .in_19(1'b0), .in_20(1'b0), .in_21(1'b0), .in_22(1'b0), .in_23(1'b0), .in_24(1'b0),
    .in_25(1'b0), .in_26(1'b0), .in_27(1'b0), .in_28(1'b0), .in_29(1'b0), .in_30(1'b0), .in_31(1'b0),
    .in_32(1'b0), .in_33(1'b0), .out_34(mux16_3_out_34), .out_35(mux16_3_out_35), .out_36(mux16_3_out_36),
    .out_37(mux16_3_out_37), .out_38(mux16_3_out_38), .out_39(mux16_3_out_39), .out_40(mux16_3_out_40),
    .out_41(mux16_3_out_41), .out_42(mux16_3_out_42), .out_43(mux16_3_out_43), .out_44(mux16_3_out_44),
    .out_45(mux16_3_out_45), .out_46(mux16_3_out_46), .out_47(mux16_3_out_47), .out_48(mux16_3_out_48),
    .out_49(mux16_3_out_49), .in_1(in_3));
  Register register_1 (
    .in_2(mux16_3_out_34), .in_3(mux16_3_out_35), .in_4(mux16_3_out_36), .in_5(mux16_3_out_37),
    .in_6(mux16_3_out_38), .in_7(mux16_3_out_39), .in_8(mux16_3_out_40), .in_9(mux16_3_out_41),
    .in_10(mux16_3_out_42), .in_11(mux16_3_out_43), .in_12(mux16_3_out_44), .in_13(mux16_3_out_45),
    .in_14(mux16_3_out_46), .in_15(mux16_3_out_47), .in_16(mux16_3_out_48), .in_17(mux16_3_out_49),
    .out_19(out_21), .out_20(out_22), .out_21(out_23), .out_22(out_24), .out_23(out_25), .out_24(out_26),
    .out_25(out_27), .out_26(out_28), .out_27(out_29), .out_28(out_30), .out_29(out_31), .out_30(out_32),
    .out_31(out_33), .out_32(out_34), .out_33(out_35), .out_34(out_36), .in_1(1'b1), .in_18(in_20));
  Inc16 inc16_1 (
    .out_18(inc16_1_out_18), .out_19(inc16_1_out_19), .out_20(inc16_1_out_20), .out_21(inc16_1_out_21),
    .out_22(inc16_1_out_22), .out_23(inc16_1_out_23), .out_24(inc16_1_out_24), .out_25(inc16_1_out_25),
    .out_26(inc16_1_out_26), .out_27(inc16_1_out_27), .out_28(inc16_1_out_28), .out_29(inc16_1_out_29),
    .out_30(inc16_1_out_30), .out_31(inc16_1_out_31), .out_32(inc16_1_out_32), .out_33(inc16_1_out_33),
    .in_1(out_21), .in_3(out_22), .in_4(out_23), .in_5(out_24), .in_6(out_25), .in_7(out_26), .in_8(out_27),
    .in_9(out_28), .in_10(out_29), .in_11(out_30), .in_12(out_31), .in_13(out_32), .in_14(out_33),
    .in_15(out_34), .in_16(out_35), .in_17(out_36), .in_2(1'b1));

  // Notes on the sheet:
  //   reset
endmodule

module DFF_1 (
  input  \清零 ,
  input  in_2,
  input  in_3,
  input  in_4,
  output out_5,
  output out_6
);

  wire n3nor_1_out_4, n3nor_2_out_4, n3nor_3_out_4, n3nor_4_out_4, not_1_out;

  not not_1 (not_1_out, in_3);
  _3NOR u_3nor_1 (.out_4(n3nor_1_out_4), .in_1(n3nor_4_out_4), .in_2(not_1_out), .in_3(n3nor_2_out_4));
  _3NOR u_3nor_2 (.out_4(n3nor_2_out_4), .in_1(n3nor_1_out_4), .in_2(in_2), .in_3(in_4));
  _3NOR u_3nor_3 (.out_4(n3nor_3_out_4), .in_1(\清零 ), .in_2(n3nor_2_out_4), .in_3(n3nor_4_out_4));
  _3NOR u_3nor_4 (.out_4(n3nor_4_out_4), .in_1(n3nor_3_out_4), .in_2(in_2), .in_3(not_1_out));
  _3NOR u_3nor_5 (.out_4(out_5), .in_1(\清零 ), .in_2(n3nor_4_out_4), .in_3(out_6));
  _3NOR u_3nor_6 (.out_4(out_6), .in_1(out_5), .in_2(in_2), .in_3(n3nor_1_out_4));

  // Notes on the sheet:
  //   预置
endmodule

module \PC_1_累了未完成  (
  input  in_1,
  input  in_2,
  input  in_3,
  input  in_4,
  input  in_5,
  input  in_6,
  input  in_7,
  input  in_8,
  input  in_9,
  input  in_10,
  input  in_11,
  input  in_12,
  input  in_13,
  input  in_14,
  input  in_15,
  input  in_16,
  input  in_17,
  input  \是否增加 ,
  input  in_19,
  output out_20,
  output out_21,
  output out_22,
  output out_23,
  output out_24,
  output out_25,
  output out_26,
  output out_27,
  output out_28,
  output out_29,
  output out_30,
  output out_31,
  output out_32,
  output out_33,
  output out_34,
  output out_35
);

  wire bit_1_out_4, clock_1_out, inc16_1_1_out_34, inc16_1_1_out_35, inc16_1_1_out_36, inc16_1_1_out_37,
       inc16_1_1_out_38, inc16_1_1_out_39, inc16_1_1_out_40, inc16_1_1_out_41, inc16_1_1_out_42,
       inc16_1_1_out_43, inc16_1_1_out_44, inc16_1_1_out_45, inc16_1_1_out_46, inc16_1_1_out_47,
       inc16_1_1_out_48, inc16_1_1_out_49, mux16_1_out_34, mux16_1_out_35, mux16_1_out_36, mux16_1_out_37,
       mux16_1_out_38, mux16_1_out_39, mux16_1_out_40, mux16_1_out_41, mux16_1_out_42, mux16_1_out_43,
       mux16_1_out_44, mux16_1_out_45, mux16_1_out_46, mux16_1_out_47, mux16_1_out_48, mux16_1_out_49,
       mux16_2_out_34, mux16_2_out_35, mux16_2_out_36, mux16_2_out_37, mux16_2_out_38, mux16_2_out_39,
       mux16_2_out_40, mux16_2_out_41, mux16_2_out_42, mux16_2_out_43, mux16_2_out_44, mux16_2_out_45,
       mux16_2_out_46, mux16_2_out_47, mux16_2_out_48, mux16_2_out_49, mux16_3_out_34, mux_1_out_4,
       mux_2_out_4, not_1_out_2, not_2_out, not_3_out_2, not_4_out_2, or_1_out_3, or_2_out_3;

  Not not_1 (.in_1(in_17), .out_2(not_1_out_2));
  Mux16 mux16_1 (
    .in_2(1'b0), .in_3(1'b0), .in_4(1'b0), .in_5(1'b0), .in_6(1'b0), .in_7(1'b0), .in_8(1'b0), .in_9(1'b0),
    .in_10(1'b0), .in_11(1'b0), .in_12(1'b0), .in_13(1'b0), .in_14(1'b0), .in_15(1'b0), .in_16(1'b0),
    .in_17(1'b0), .in_18(1'b1), .in_19(1'b1), .in_20(1'b1), .in_21(1'b1), .in_22(1'b1), .in_23(1'b1),
    .in_24(1'b1), .in_25(1'b1), .in_26(1'b1), .in_27(1'b1), .in_28(1'b1), .in_29(1'b1), .in_30(1'b1),
    .in_31(1'b1), .in_32(1'b1), .in_33(1'b1), .out_34(mux16_1_out_34), .out_35(mux16_1_out_35),
    .out_36(mux16_1_out_36), .out_37(mux16_1_out_37), .out_38(mux16_1_out_38), .out_39(mux16_1_out_39),
    .out_40(mux16_1_out_40), .out_41(mux16_1_out_41), .out_42(mux16_1_out_42), .out_43(mux16_1_out_43),
    .out_44(mux16_1_out_44), .out_45(mux16_1_out_45), .out_46(mux16_1_out_46), .out_47(mux16_1_out_47),
    .out_48(mux16_1_out_48), .out_49(mux16_1_out_49), .in_1(in_17));
  Inc16_1 inc16_1_1 (
    .out_34(inc16_1_1_out_34), .out_35(inc16_1_1_out_35), .out_36(inc16_1_1_out_36),
    .out_37(inc16_1_1_out_37), .out_38(inc16_1_1_out_38), .out_39(inc16_1_1_out_39),
    .out_40(inc16_1_1_out_40), .out_41(inc16_1_1_out_41), .out_42(inc16_1_1_out_42),
    .out_43(inc16_1_1_out_43), .out_44(inc16_1_1_out_44), .out_45(inc16_1_1_out_45),
    .out_46(inc16_1_1_out_46), .out_47(inc16_1_1_out_47), .out_48(inc16_1_1_out_48),
    .out_49(inc16_1_1_out_49), .in_1(mux16_1_out_49), .in_2(mux16_1_out_48), .in_3(mux16_1_out_47),
    .in_4(mux16_1_out_46), .in_5(mux16_1_out_45), .in_6(mux16_1_out_44), .in_7(mux16_1_out_43),
    .in_8(mux16_1_out_42), .in_9(mux16_1_out_41), .in_10(mux16_1_out_40), .in_11(mux16_1_out_39),
    .in_12(mux16_1_out_38), .in_13(mux16_1_out_37), .in_14(mux16_1_out_36), .in_15(mux16_1_out_35),
    .in_16(mux16_1_out_34), .in_18(mux_2_out_4), .in_19(mux16_2_out_35), .in_20(mux16_2_out_36),
    .in_21(mux16_2_out_37), .in_22(mux16_2_out_38), .in_23(mux16_2_out_39), .in_24(mux16_2_out_40),
    .in_25(mux16_2_out_41), .in_26(mux16_2_out_42), .in_27(mux16_2_out_43), .in_28(mux16_2_out_44),
    .in_29(mux16_2_out_45), .in_30(mux16_2_out_46), .in_31(mux16_2_out_47), .in_32(mux16_2_out_48),
    .in_33(mux16_2_out_49), .in_17(clock_1_out));
  Clock clock_1 (.out(clock_1_out));
  Mux16 mux16_2 (
    .in_2(1'b0), .in_3(1'b0), .in_4(1'b0), .in_5(1'b0), .in_6(1'b0), .in_7(1'b0), .in_8(1'b0), .in_9(1'b0),
    .in_10(1'b0), .in_11(1'b0), .in_12(1'b0), .in_13(1'b0), .in_14(1'b0), .in_15(1'b0), .in_16(1'b0),
    .in_17(1'b0), .in_18(in_1), .in_19(in_2), .in_20(in_3), .in_21(in_4), .in_22(in_5), .in_23(in_6),
    .in_24(in_7), .in_25(in_8), .in_26(in_9), .in_27(in_10), .in_28(in_11), .in_29(in_12), .in_30(in_13),
    .in_31(in_14), .in_32(in_15), .in_33(in_16), .out_34(mux16_2_out_34), .out_35(mux16_2_out_35),
    .out_36(mux16_2_out_36), .out_37(mux16_2_out_37), .out_38(mux16_2_out_38), .out_39(mux16_2_out_39),
    .out_40(mux16_2_out_40), .out_41(mux16_2_out_41), .out_42(mux16_2_out_42), .out_43(mux16_2_out_43),
    .out_44(mux16_2_out_44), .out_45(mux16_2_out_45), .out_46(mux16_2_out_46), .out_47(mux16_2_out_47),
    .out_48(mux16_2_out_48), .out_49(mux16_2_out_49), .in_1(\是否增加 ));
  Mux mux_1 (.in_2(mux16_2_out_34), .in_3(or_2_out_3), .out_4(mux_1_out_4), .in_1(or_1_out_3));
  Mux mux_2 (.in_2(1'b0), .in_3(mux_1_out_4), .out_4(mux_2_out_4), .in_1(or_1_out_3));
  not not_2 (not_2_out, in_19);
  OR or_1 (.in_1(not_2_out), .in_2(\是否增加 ), .out_3(or_1_out_3));
  Bit bit_1 (.out_4(bit_1_out_4), .in_1(not_3_out_2), .in_2(inc16_1_1_out_34), .in_3(clock_1_out));
  Not not_3 (.in_1(not_2_out), .out_2(not_3_out_2));
  OR or_2 (.in_1(1'b1), .in_2(inc16_1_1_out_34), .out_3(or_2_out_3));
  Not not_4 (.in_1(bit_1_out_4), .out_2(not_4_out_2));
  Mux16 mux16_3 (
    .in_2(not_4_out_2), .in_3(inc16_1_1_out_35), .in_4(inc16_1_1_out_36), .in_5(inc16_1_1_out_37),
    .in_6(inc16_1_1_out_38), .in_7(inc16_1_1_out_39), .in_8(inc16_1_1_out_40), .in_9(inc16_1_1_out_41),
    .in_10(inc16_1_1_out_42), .in_11(inc16_1_1_out_43), .in_12(inc16_1_1_out_44), .in_13(inc16_1_1_out_45),
    .in_14(inc16_1_1_out_46), .in_15(inc16_1_1_out_47), .in_16(inc16_1_1_out_48), .in_17(inc16_1_1_out_49),
    .in_18(in_1), .in_19(in_2), .in_20(in_3), .in_21(in_4), .in_22(in_5), .in_23(in_6), .in_24(in_7),
    .in_25(in_8), .in_26(in_9), .in_27(in_10), .in_28(in_11), .in_29(in_12), .in_30(in_13), .in_31(in_14),
    .in_32(in_15), .in_33(in_16), .out_34(mux16_3_out_34), .out_35(out_21), .out_36(out_22), .out_37(out_23),
    .out_38(out_24), .out_39(out_25), .out_40(out_26), .out_41(out_27), .out_42(out_28), .out_43(out_29),
    .out_44(out_30), .out_45(out_31), .out_46(out_32), .out_47(out_33), .out_48(out_34), .out_49(out_35),
    .in_1(\是否增加 ));
  Mux mux_3 (.in_2(1'b0), .in_3(mux16_3_out_34), .out_4(out_20), .in_1(not_1_out_2));

  // Notes on the sheet:
  //   是否预置
endmodule

module Inc16_1 (
  input  in_1,
  input  in_2,
  input  in_3,
  input  in_4,
  input  in_5,
  input  in_6,
  input  in_7,
  input  in_8,
  input  in_9,
  input  in_10,
  input  in_11,
  input  in_12,
  input  in_13,
  input  in_14,
  input  in_15,
  input  in_16,
  input  in_17,
  input  in_18,
  input  in_19,
  input  in_20,
  input  in_21,
  input  in_22,
  input  in_23,
  input  in_24,
  input  in_25,
  input  in_26,
  input  in_27,
  input  in_28,
  input  in_29,
  input  in_30,
  input  in_31,
  input  in_32,
  input  in_33,
  output out_34,
  output out_35,
  output out_36,
  output out_37,
  output out_38,
  output out_39,
  output out_40,
  output out_41,
  output out_42,
  output out_43,
  output out_44,
  output out_45,
  output out_46,
  output out_47,
  output out_48,
  output out_49
);

  wire dff_1_1_out_6, dff_1_2_out_6, dff_1_3_out_6, dff_1_4_out_6, dff_1_5_out_6, dff_1_6_out_6,
       dff_1_7_out_6, dff_1_8_out_6, dff_1_9_out_6, dff_1_10_out_6, dff_1_11_out_6, dff_1_12_out_6,
       dff_1_13_out_6, dff_1_14_out_6, dff_1_15_out_6, dff_1_16_out_6;

  DFF_1 dff_1_1 (.in_4(dff_1_1_out_6), .out_5(out_34), .out_6(dff_1_1_out_6), .\清零 (in_1), .in_2(in_18), .in_3(in_17));
  DFF_1 dff_1_2 (
    .in_4(dff_1_2_out_6), .out_5(out_35), .out_6(dff_1_2_out_6), .\清零 (in_2), .in_2(in_19),
    .in_3(dff_1_1_out_6));
  DFF_1 dff_1_3 (
    .in_4(dff_1_3_out_6), .out_5(out_36), .out_6(dff_1_3_out_6), .\清零 (in_3), .in_2(in_20),
    .in_3(dff_1_2_out_6));
  DFF_1 dff_1_4 (
    .in_4(dff_1_4_out_6), .out_5(out_37), .out_6(dff_1_4_out_6), .\清零 (in_4), .in_2(in_21),
    .in_3(dff_1_3_out_6));
  DFF_1 dff_1_5 (
    .in_4(dff_1_5_out_6), .out_5(out_38), .out_6(dff_1_5_out_6), .\清零 (in_5), .in_2(in_22),
    .in_3(dff_1_4_out_6));
  DFF_1 dff_1_6 (
    .in_4(dff_1_6_out_6), .out_5(out_39), .out_6(dff_1_6_out_6), .\清零 (in_6), .in_2(in_23),
    .in_3(dff_1_5_out_6));
  DFF_1 dff_1_7 (
    .in_4(dff_1_7_out_6), .out_5(out_40), .out_6(dff_1_7_out_6), .\清零 (in_7), .in_2(in_24),
    .in_3(dff_1_6_out_6));
  DFF_1 dff_1_8 (
    .in_4(dff_1_8_out_6), .out_5(out_41), .out_6(dff_1_8_out_6), .\清零 (in_8), .in_2(in_25),
    .in_3(dff_1_7_out_6));
  DFF_1 dff_1_9 (
    .in_4(dff_1_9_out_6), .out_5(out_42), .out_6(dff_1_9_out_6), .\清零 (in_9), .in_2(in_26),
    .in_3(dff_1_8_out_6));
  DFF_1 dff_1_10 (
    .in_4(dff_1_10_out_6), .out_5(out_43), .out_6(dff_1_10_out_6), .\清零 (in_10), .in_2(in_27),
    .in_3(dff_1_9_out_6));
  DFF_1 dff_1_11 (
    .in_4(dff_1_11_out_6), .out_5(out_44), .out_6(dff_1_11_out_6), .\清零 (in_11), .in_2(in_28),
    .in_3(dff_1_10_out_6));
  DFF_1 dff_1_12 (
    .in_4(dff_1_12_out_6), .out_5(out_45), .out_6(dff_1_12_out_6), .\清零 (in_12), .in_2(in_29),
    .in_3(dff_1_11_out_6));
  DFF_1 dff_1_13 (
    .in_4(dff_1_13_out_6), .out_5(out_46), .out_6(dff_1_13_out_6), .\清零 (in_13), .in_2(in_30),
    .in_3(dff_1_12_out_6));
  DFF_1 dff_1_14 (
    .in_4(dff_1_14_out_6), .out_5(out_47), .out_6(dff_1_14_out_6), .\清零 (in_14), .in_2(in_31),
    .in_3(dff_1_13_out_6));
  DFF_1 dff_1_15 (
    .in_4(dff_1_15_out_6), .out_5(out_48), .out_6(dff_1_15_out_6), .\清零 (in_15), .in_2(in_32),
    .in_3(dff_1_14_out_6));
  DFF_1 dff_1_16 (
    .in_4(dff_1_16_out_6), .out_5(out_49), .out_6(dff_1_16_out_6), .\清零 (in_16), .in_2(in_33),
    .in_3(dff_1_15_out_6));
endmodule

module \DMux8Way_修改了引脚  (
  input  in_1,
  input  in_2,
  input  in_3,
  input  [15:0] in_4,
  output [15:0] out_5,
  output [15:0] out_6,
  output [15:0] out_7,
  output [15:0] out_8,
  output [15:0] out_9,
  output [15:0] out_10,
  output [15:0] out_11,
  output [15:0] out_12
);

  wire [15:0] \dmux_修改了引脚_1_out_3 , \dmux_修改了引脚_1_out_4 ;

  \DMux_修改了引脚  \dmux_修改了引脚_1  (.in_2(in_4), .out_3(\dmux_修改了引脚_1_out_3 ), .out_4(\dmux_修改了引脚_1_out_4 ), .in_1(in_1));
  \DMux4Way_修改了引脚  \dmux4way_修改了引脚_1  (
    .out_4(out_5), .out_5(out_6), .out_6(out_7), .out_7(out_8), .in_1(in_2), .in_2(in_3),
    .in_3(\dmux_修改了引脚_1_out_3 ));
  \DMux4Way_修改了引脚  \dmux4way_修改了引脚_2  (
    .out_4(out_9), .out_5(out_10), .out_6(out_11), .out_7(out_12), .in_1(in_2), .in_2(in_3),
    .in_3(\dmux_修改了引脚_1_out_4 ));
endmodule
module \DMux4Way_修改了引脚  (
  input  in_1,
  input  in_2,
  input  [15:0] in_3,
  output [15:0] out_4,
  output [15:0] out_5,
  output [15:0] out_6,
  output [15:0] out_7
);

  wire not_1_out_2, not_2_out_2;
  wire [15:15] and_1_out_3, and_2_out_3, and_3_out_3, and_4_out_3;

  Not not_1 (.in_1(in_1), .out_2(not_1_out_2));
  Not not_2 (.in_1(in_2), .out_2(not_2_out_2));
  AND and_1 (.in_1(not_1_out_2), .in_2(not_2_out_2), .out_3(and_1_out_3[15]));
  AND and_2 (.in_1(not_1_out_2), .in_2(in_2), .out_3(and_2_out_3[15]));
  AND and_3 (.in_1(in_1), .in_2(not_2_out_2), .out_3(and_3_out_3[15]));
  AND and_4 (.in_1(in_1), .in_2(in_2), .out_3(and_4_out_3[15]));
  \AND_修改了引脚  \and_修改了引脚_1  (.in_1({16{and_1_out_3[15]}}), .in_2(in_3), .out_3(out_4));
  \AND_修改了引脚  \and_修改了引脚_2  (.in_1({16{and_2_out_3[15]}}), .in_2(in_3), .out_3(out_5));
  \AND_修改了引脚  \and_修改了引脚_3  (.in_1({16{and_3_out_3[15]}}), .in_2(in_3), .out_3(out_6));
  \AND_修改了引脚  \and_修改了引脚_4  (.in_1({16{and_4_out_3[15]}}), .in_2(in_3), .out_3(out_7));

  // Notes on the sheet:
  //   sel-0
  //   sel-1
endmodule

module \AND_修改了引脚  (
  input  [15:0] in_1,
  input  [15:0] in_2,
  output [15:0] out_3
);

  wire [15:0] nand_1_out;

  assign nand_1_out = ~(in_1 & in_2);  // NAND_Gate nand_1, 16 bits wide
  assign out_3 = ~(nand_1_out & nand_1_out);  // NAND_Gate nand_2, 16 bits wide
endmodule

module \DMux_修改了引脚  (
  input  in_1,
  input  [15:0] in_2,
  output [15:0] out_3,
  output [15:0] out_4
);

  wire [15:15] not_1_out_2;

  Not not_1 (.in_1(in_1), .out_2(not_1_out_2[15]));
  \AND_修改了引脚  \and_修改了引脚_1  (.in_1({16{not_1_out_2[15]}}), .in_2(in_2), .out_3(out_3));
  \AND_修改了引脚  \and_修改了引脚_2  (.in_1({16{in_1}}), .in_2(in_2), .out_3(out_4));
endmodule

module \OR16_修改引脚  (
  input  [15:0] in_1,
  input  [15:0] in_2,
  output [15:0] out_3
);

  wire [15:0] nand_1_out, nand_2_out;

  assign nand_1_out = ~(in_1 & in_1);  // NAND_Gate nand_1, 16 bits wide
  assign nand_2_out = ~(in_2 & in_2);  // NAND_Gate nand_2, 16 bits wide
  assign out_3 = ~(nand_1_out & nand_2_out);  // NAND_Gate nand_3, 16 bits wide
endmodule

module \Mux16_修改了引脚  (
  input  in_1,
  input  [15:0] in_2,
  input  [15:0] in_3,
  output [15:0] out_4
);

  wire [15:0] \and_修改了引脚_1_out_3 , \and_修改了引脚_2_out_3 , \not16_修改引脚_1_out_2 ;

  \not16_修改引脚  \not16_修改引脚_1  (.in_1({16{in_1}}), .out_2(\not16_修改引脚_1_out_2 ));
  \AND_修改了引脚  \and_修改了引脚_1  (.in_1(\not16_修改引脚_1_out_2 ), .in_2(in_2), .out_3(\and_修改了引脚_1_out_3 ));
  \AND_修改了引脚  \and_修改了引脚_2  (.in_1({16{in_1}}), .in_2(in_3), .out_3(\and_修改了引脚_2_out_3 ));
  \OR16_修改引脚  \or16_修改引脚_1  (.in_1(\and_修改了引脚_1_out_3 ), .in_2(\and_修改了引脚_2_out_3 ), .out_3(out_4));
endmodule

module \not16_修改引脚  (
  input  [15:0] in_1,
  output [15:0] out_2
);

  assign out_2 = ~(in_1 & in_1);  // NAND_Gate nand_1, 16 bits wide
endmodule

module \Mux4Way16_修改了引脚  (
  input  in_1,
  input  in_2,
  input  [15:0] in_3,
  input  [15:0] in_4,
  input  [15:0] in_5,
  input  [15:0] in_6,
  output [15:0] out_7
);

  wire [15:0] \and_修改了引脚_1_out_3 , \and_修改了引脚_2_out_3 , \mux16_修改了引脚_1_out_4 , \mux16_修改了引脚_2_out_4 ,
       \not16_修改引脚_1_out_2 ;

  \Mux16_修改了引脚  \mux16_修改了引脚_1  (.in_2(in_3), .in_3(in_4), .out_4(\mux16_修改了引脚_1_out_4 ), .in_1(in_2));
  \Mux16_修改了引脚  \mux16_修改了引脚_2  (.in_2(in_5), .in_3(in_6), .out_4(\mux16_修改了引脚_2_out_4 ), .in_1(in_2));
  \not16_修改引脚  \not16_修改引脚_1  (.in_1({16{in_1}}), .out_2(\not16_修改引脚_1_out_2 ));
  \AND_修改了引脚  \and_修改了引脚_1  (.in_1(\not16_修改引脚_1_out_2 ), .in_2(\mux16_修改了引脚_1_out_4 ), .out_3(\and_修改了引脚_1_out_3 ));
  \AND_修改了引脚  \and_修改了引脚_2  (.in_1({16{in_1}}), .in_2(\mux16_修改了引脚_2_out_4 ), .out_3(\and_修改了引脚_2_out_3 ));
  \OR16_修改引脚  \or16_修改引脚_1  (.in_1(\and_修改了引脚_1_out_3 ), .in_2(\and_修改了引脚_2_out_3 ), .out_3(out_7));
endmodule

module \Mux8Way16_修改了引脚  (
  input  in_1,
  input  in_2,
  input  in_3,
  input  [15:0] in_4,
  input  [15:0] in_5,
  input  [15:0] in_6,
  input  [15:0] in_7,
  input  [15:0] in_8,
  input  [15:0] in_9,
  input  [15:0] in_10,
  input  [15:0] in_11,
  output [15:0] out_12
);

  wire [15:0] \mux4way16_修改了引脚_1_out_7 , \mux4way16_修改了引脚_2_out_7 ;

  \Mux4Way16_修改了引脚  \mux4way16_修改了引脚_1  (
    .in_3(in_4), .in_4(in_5), .in_5(in_6), .in_6(in_7), .out_7(\mux4way16_修改了引脚_1_out_7 ), .in_1(in_2),
    .in_2(in_3));
  \Mux4Way16_修改了引脚  \mux4way16_修改了引脚_2  (
    .in_3(in_8), .in_4(in_9), .in_5(in_10), .in_6(in_11), .out_7(\mux4way16_修改了引脚_2_out_7 ), .in_1(in_2),
    .in_2(in_3));
  \Mux16_修改了引脚  \mux16_修改了引脚_1  (
    .in_2(\mux4way16_修改了引脚_1_out_7 ), .in_3(\mux4way16_修改了引脚_2_out_7 ), .out_4(out_12), .in_1(in_1));
endmodule

module \RAM8_修改了引脚_采用内置寄存器  (
  input  in_1,
  input  in_2,
  input  in_3,
  input  in_4,
  input  [15:0] in_5,
  input  in_6,
  output [15:0] out_7
);

  wire dmux8way_1_out_5, dmux8way_1_out_6, dmux8way_1_out_7, dmux8way_1_out_8, dmux8way_1_out_9,
       dmux8way_1_out_10, dmux8way_1_out_11, dmux8way_1_out_12;
  wire [15:0] register_1_q, register_2_q, register_3_q, register_4_q, register_5_q, register_6_q,
       register_7_q, register_8_q;

  Register_part #(.width(16)) register_1 (.D(in_5), .en(dmux8way_1_out_12), .Q(register_1_q), .clk(in_6));  // open: clr
  Register_part #(.width(16)) register_2 (.D(in_5), .en(dmux8way_1_out_11), .Q(register_2_q), .clk(in_6));  // open: clr
  Register_part #(.width(16)) register_3 (.D(in_5), .en(dmux8way_1_out_10), .Q(register_3_q), .clk(in_6));  // open: clr
  Register_part #(.width(16)) register_4 (.D(in_5), .en(dmux8way_1_out_9), .Q(register_4_q), .clk(in_6));  // open: clr
  Register_part #(.width(16)) register_5 (.D(in_5), .en(dmux8way_1_out_8), .Q(register_5_q), .clk(in_6));  // open: clr
  Register_part #(.width(16)) register_6 (.D(in_5), .en(dmux8way_1_out_6), .Q(register_6_q), .clk(in_6));  // open: clr
  Register_part #(.width(16)) register_7 (.D(in_5), .en(dmux8way_1_out_7), .Q(register_7_q), .clk(in_6));  // open: clr
  Register_part #(.width(16)) register_8 (.D(in_5), .en(dmux8way_1_out_5), .Q(register_8_q), .clk(in_6));  // open: clr
  DMux8Way dmux8way_1 (
    .in_4(in_1), .out_5(dmux8way_1_out_5), .out_6(dmux8way_1_out_6), .out_7(dmux8way_1_out_7),
    .out_8(dmux8way_1_out_8), .out_9(dmux8way_1_out_9), .out_10(dmux8way_1_out_10),
    .out_11(dmux8way_1_out_11), .out_12(dmux8way_1_out_12), .in_1(in_2), .in_2(in_3), .in_3(in_4));
  \Mux8Way16_修改了引脚  \mux8way16_修改了引脚_1  (
    .in_4(register_8_q), .in_5(register_6_q), .in_6(register_7_q), .in_7(register_5_q), .in_8(register_4_q),
    .in_9(register_3_q), .in_10(register_2_q), .in_11(register_1_q), .out_12(out_7), .in_1(in_2),
    .in_2(in_3), .in_3(in_4));
endmodule

module \RAM64_修改了引脚_采用内置寄存器  (
  input  in_1,
  input  in_2,
  input  in_3,
  input  in_4,
  input  in_5,
  input  in_6,
  input  in_7,
  input  [15:0] in_8,
  input  in_9,
  output [15:0] out_10
);

  wire dmux8way_1_out_5, dmux8way_1_out_6, dmux8way_1_out_7, dmux8way_1_out_8, dmux8way_1_out_9,
       dmux8way_1_out_10, dmux8way_1_out_11, dmux8way_1_out_12;
  wire [15:0] \ram8_修改了引脚_采用内置寄存器_1_out_7 , \ram8_修改了引脚_采用内置寄存器_2_out_7 , \ram8_修改了引脚_采用内置寄存器_3_out_7 ,
       \ram8_修改了引脚_采用内置寄存器_4_out_7 , \ram8_修改了引脚_采用内置寄存器_5_out_7 , \ram8_修改了引脚_采用内置寄存器_6_out_7 ,
       \ram8_修改了引脚_采用内置寄存器_7_out_7 , \ram8_修改了引脚_采用内置寄存器_8_out_7 ;

  \RAM8_修改了引脚_采用内置寄存器  \ram8_修改了引脚_采用内置寄存器_1  (
    .in_5(in_8), .out_7(\ram8_修改了引脚_采用内置寄存器_1_out_7 ), .in_1(dmux8way_1_out_12), .in_2(in_5), .in_3(in_6),
    .in_4(in_7), .in_6(in_9));
  \RAM8_修改了引脚_采用内置寄存器  \ram8_修改了引脚_采用内置寄存器_2  (
    .in_5(in_8), .out_7(\ram8_修改了引脚_采用内置寄存器_2_out_7 ), .in_1(dmux8way_1_out_11), .in_2(in_5), .in_3(in_6),
    .in_4(in_7), .in_6(in_9));
  \RAM8_修改了引脚_采用内置寄存器  \ram8_修改了引脚_采用内置寄存器_3  (
    .in_5(in_8), .out_7(\ram8_修改了引脚_采用内置寄存器_3_out_7 ), .in_1(dmux8way_1_out_10), .in_2(in_5), .in_3(in_6),
    .in_4(in_7), .in_6(in_9));
  \RAM8_修改了引脚_采用内置寄存器  \ram8_修改了引脚_采用内置寄存器_4  (
    .in_5(in_8), .out_7(\ram8_修改了引脚_采用内置寄存器_4_out_7 ), .in_1(dmux8way_1_out_9), .in_2(in_5), .in_3(in_6),
    .in_4(in_7), .in_6(in_9));
  \RAM8_修改了引脚_采用内置寄存器  \ram8_修改了引脚_采用内置寄存器_5  (
    .in_5(in_8), .out_7(\ram8_修改了引脚_采用内置寄存器_5_out_7 ), .in_1(dmux8way_1_out_8), .in_2(in_5), .in_3(in_6),
    .in_4(in_7), .in_6(in_9));
  \RAM8_修改了引脚_采用内置寄存器  \ram8_修改了引脚_采用内置寄存器_6  (
    .in_5(in_8), .out_7(\ram8_修改了引脚_采用内置寄存器_6_out_7 ), .in_1(dmux8way_1_out_7), .in_2(in_5), .in_3(in_6),
    .in_4(in_7), .in_6(in_9));
  \RAM8_修改了引脚_采用内置寄存器  \ram8_修改了引脚_采用内置寄存器_7  (
    .in_5(in_8), .out_7(\ram8_修改了引脚_采用内置寄存器_7_out_7 ), .in_1(dmux8way_1_out_6), .in_2(in_5), .in_3(in_6),
    .in_4(in_7), .in_6(in_9));
  \RAM8_修改了引脚_采用内置寄存器  \ram8_修改了引脚_采用内置寄存器_8  (
    .in_5(in_8), .out_7(\ram8_修改了引脚_采用内置寄存器_8_out_7 ), .in_1(dmux8way_1_out_5), .in_2(in_5), .in_3(in_6),
    .in_4(in_7), .in_6(in_9));
  DMux8Way dmux8way_1 (
    .in_4(in_1), .out_5(dmux8way_1_out_5), .out_6(dmux8way_1_out_6), .out_7(dmux8way_1_out_7),
    .out_8(dmux8way_1_out_8), .out_9(dmux8way_1_out_9), .out_10(dmux8way_1_out_10),
    .out_11(dmux8way_1_out_11), .out_12(dmux8way_1_out_12), .in_1(in_2), .in_2(in_3), .in_3(in_4));
  \Mux8Way16_修改了引脚  \mux8way16_修改了引脚_1  (
    .in_4(\ram8_修改了引脚_采用内置寄存器_8_out_7 ), .in_5(\ram8_修改了引脚_采用内置寄存器_7_out_7 ),
    .in_6(\ram8_修改了引脚_采用内置寄存器_6_out_7 ), .in_7(\ram8_修改了引脚_采用内置寄存器_5_out_7 ),
    .in_8(\ram8_修改了引脚_采用内置寄存器_4_out_7 ), .in_9(\ram8_修改了引脚_采用内置寄存器_3_out_7 ),
    .in_10(\ram8_修改了引脚_采用内置寄存器_2_out_7 ), .in_11(\ram8_修改了引脚_采用内置寄存器_1_out_7 ), .out_12(out_10), .in_1(in_2),
    .in_2(in_3), .in_3(in_4));
endmodule

module \RAM512_修改了引脚_采用内置寄存器  (
  input  in_1,
  input  in_2,
  input  in_3,
  input  in_4,
  input  in_5,
  input  in_6,
  input  in_7,
  input  in_8,
  input  in_9,
  input  in_10,
  input  [15:0] in_11,
  input  in_12,
  output [15:0] out_13
);

  wire dmux8way_1_out_5, dmux8way_1_out_6, dmux8way_1_out_7, dmux8way_1_out_8, dmux8way_1_out_9,
       dmux8way_1_out_10, dmux8way_1_out_11, dmux8way_1_out_12;
  wire [15:0] \ram64_修改了引脚_采用内置寄存器_1_out_10 , \ram64_修改了引脚_采用内置寄存器_2_out_10 , \ram64_修改了引脚_采用内置寄存器_3_out_10 ,
       \ram64_修改了引脚_采用内置寄存器_4_out_10 , \ram64_修改了引脚_采用内置寄存器_5_out_10 , \ram64_修改了引脚_采用内置寄存器_6_out_10 ,
       \ram64_修改了引脚_采用内置寄存器_7_out_10 , \ram64_修改了引脚_采用内置寄存器_8_out_10 ;

  \RAM64_修改了引脚_采用内置寄存器  \ram64_修改了引脚_采用内置寄存器_1  (
    .in_8(in_11), .out_10(\ram64_修改了引脚_采用内置寄存器_1_out_10 ), .in_1(dmux8way_1_out_12), .in_2(in_5),
    .in_3(in_6), .in_4(in_7), .in_5(in_8), .in_6(in_9), .in_7(in_10), .in_9(in_12));
  \RAM64_修改了引脚_采用内置寄存器  \ram64_修改了引脚_采用内置寄存器_2  (
    .in_8(in_11), .out_10(\ram64_修改了引脚_采用内置寄存器_2_out_10 ), .in_1(dmux8way_1_out_11), .in_2(in_5),
    .in_3(in_6), .in_4(in_7), .in_5(in_8), .in_6(in_9), .in_7(in_10), .in_9(in_12));
  \RAM64_修改了引脚_采用内置寄存器  \ram64_修改了引脚_采用内置寄存器_3  (
    .in_8(in_11), .out_10(\ram64_修改了引脚_采用内置寄存器_3_out_10 ), .in_1(dmux8way_1_out_10), .in_2(in_5),
    .in_3(in_6), .in_4(in_7), .in_5(in_8), .in_6(in_9), .in_7(in_10), .in_9(in_12));
  \RAM64_修改了引脚_采用内置寄存器  \ram64_修改了引脚_采用内置寄存器_4  (
    .in_8(in_11), .out_10(\ram64_修改了引脚_采用内置寄存器_4_out_10 ), .in_1(dmux8way_1_out_9), .in_2(in_5), .in_3(in_6),
    .in_4(in_7), .in_5(in_8), .in_6(in_9), .in_7(in_10), .in_9(in_12));
  \RAM64_修改了引脚_采用内置寄存器  \ram64_修改了引脚_采用内置寄存器_5  (
    .in_8(in_11), .out_10(\ram64_修改了引脚_采用内置寄存器_5_out_10 ), .in_1(dmux8way_1_out_8), .in_2(in_5), .in_3(in_6),
    .in_4(in_7), .in_5(in_8), .in_6(in_9), .in_7(in_10), .in_9(in_12));
  \RAM64_修改了引脚_采用内置寄存器  \ram64_修改了引脚_采用内置寄存器_6  (
    .in_8(in_11), .out_10(\ram64_修改了引脚_采用内置寄存器_6_out_10 ), .in_1(dmux8way_1_out_7), .in_2(in_5), .in_3(in_6),
    .in_4(in_7), .in_5(in_8), .in_6(in_9), .in_7(in_10), .in_9(in_12));
  \RAM64_修改了引脚_采用内置寄存器  \ram64_修改了引脚_采用内置寄存器_7  (
    .in_8(in_11), .out_10(\ram64_修改了引脚_采用内置寄存器_7_out_10 ), .in_1(dmux8way_1_out_6), .in_2(in_5), .in_3(in_6),
    .in_4(in_7), .in_5(in_8), .in_6(in_9), .in_7(in_10), .in_9(in_12));
  \RAM64_修改了引脚_采用内置寄存器  \ram64_修改了引脚_采用内置寄存器_8  (
    .in_8(in_11), .out_10(\ram64_修改了引脚_采用内置寄存器_8_out_10 ), .in_1(dmux8way_1_out_5), .in_2(in_5), .in_3(in_6),
    .in_4(in_7), .in_5(in_8), .in_6(in_9), .in_7(in_10), .in_9(in_12));
  DMux8Way dmux8way_1 (
    .in_4(in_1), .out_5(dmux8way_1_out_5), .out_6(dmux8way_1_out_6), .out_7(dmux8way_1_out_7),
    .out_8(dmux8way_1_out_8), .out_9(dmux8way_1_out_9), .out_10(dmux8way_1_out_10),
    .out_11(dmux8way_1_out_11), .out_12(dmux8way_1_out_12), .in_1(in_2), .in_2(in_3), .in_3(in_4));
  \Mux8Way16_修改了引脚  \mux8way16_修改了引脚_1  (
    .in_4(\ram64_修改了引脚_采用内置寄存器_8_out_10 ), .in_5(\ram64_修改了引脚_采用内置寄存器_7_out_10 ),
    .in_6(\ram64_修改了引脚_采用内置寄存器_6_out_10 ), .in_7(\ram64_修改了引脚_采用内置寄存器_5_out_10 ),
    .in_8(\ram64_修改了引脚_采用内置寄存器_4_out_10 ), .in_9(\ram64_修改了引脚_采用内置寄存器_3_out_10 ),
    .in_10(\ram64_修改了引脚_采用内置寄存器_2_out_10 ), .in_11(\ram64_修改了引脚_采用内置寄存器_1_out_10 ), .out_12(out_13),
    .in_1(in_2), .in_2(in_3), .in_3(in_4));
endmodule

module \RAM4K_已极限_傻鸟Java软件的极限_不是我的极限_使用三态门_采用内置RAM  (
  input  [15:0] in_1,
  input  [11:0] in_2,
  input  in_3,
  input  in_4,
  output [15:0] out_5
);

  wire not_1_out_2;

  assign out_5 = not_1_out_2 ? in_1 : 16'bz;  // Controlled_Buffer controlled_buffer_1
  Not not_1 (.in_1(in_4), .out_2(not_1_out_2));
  RAM #(.addrWidth(12), .dataWidth(16)) ram_1 (.addr(in_2), .data(out_5), .clk(in_3), .ld(in_4));  // open: sel, clr
endmodule

module RAM8k (
  input  [15:0] in_1,
  input  [12:0] in_2,
  input  in_3,
  input  in_4,
  output [15:0] out_5
);

  wire not_1_out_2;

  assign out_5 = in_3 ? in_1 : 16'bz;  // Controlled_Buffer controlled_buffer_1
  Not not_1 (.in_1(in_3), .out_2(not_1_out_2));
  RAM #(.addrWidth(13), .dataWidth(16)) ram_1 (
    .addr(in_2), .data(out_5), .clk(in_4), .ld(not_1_out_2));  // open: sel, clr
endmodule

module \RAM16K_使用三态门_采用内置RAM  (
  input  [15:0] in_1,
  input  [13:0] in_2,
  input  in_3,
  input  in_4,
  output [15:0] out_5
);

  wire not_1_out_2;

  assign out_5 = in_3 ? in_1 : 16'bz;  // Controlled_Buffer controlled_buffer_1
  Not not_1 (.in_1(in_3), .out_2(not_1_out_2));
  RAM #(.addrWidth(14), .dataWidth(16)) ram_1 (
    .addr(in_2), .data(out_5), .clk(in_4), .ld(not_1_out_2));  // open: sel, clr
endmodule

module \ALU_采用了内置加法器_修改了引脚  (
  input  in_1,
  input  in_2,
  input  in_3,
  input  in_4,
  input  [15:0] in_5,
  input  in_6,
  input  in_7,
  input  [15:0] in_8,
  output [15:0] out_9,
  output out_10,
  output out_11
);

  wire or8way_1_out_9, or8way_2_out_9, or_1_out_3;
  wire [15:0] adder_1_out, \and_修改了引脚_1_out_3 , \mux16_修改了引脚_1_out_4 , \mux16_修改了引脚_2_out_4 ,
       \mux16_修改了引脚_3_out_4 , \mux16_修改了引脚_4_out_4 , \mux16_修改了引脚_5_out_4 , \not16_修改引脚_1_out_2 ,
       \not16_修改引脚_2_out_2 , \not16_修改引脚_3_out_2 ;

  \Mux16_修改了引脚  \mux16_修改了引脚_1  (.in_2(in_5), .in_3({16{1'b0}}), .out_4(\mux16_修改了引脚_1_out_4 ), .in_1(in_1));
  \Mux16_修改了引脚  \mux16_修改了引脚_2  (.in_2(in_8), .in_3({16{1'b0}}), .out_4(\mux16_修改了引脚_2_out_4 ), .in_1(in_6));
  \Mux16_修改了引脚  \mux16_修改了引脚_3  (
    .in_2(\mux16_修改了引脚_1_out_4 ), .in_3(\not16_修改引脚_1_out_2 ), .out_4(\mux16_修改了引脚_3_out_4 ), .in_1(in_2));
  \not16_修改引脚  \not16_修改引脚_1  (.in_1(\mux16_修改了引脚_1_out_4 ), .out_2(\not16_修改引脚_1_out_2 ));
  \Mux16_修改了引脚  \mux16_修改了引脚_4  (
    .in_2(\mux16_修改了引脚_2_out_4 ), .in_3(\not16_修改引脚_2_out_2 ), .out_4(\mux16_修改了引脚_4_out_4 ), .in_1(in_7));
  \not16_修改引脚  \not16_修改引脚_2  (.in_1(\mux16_修改了引脚_2_out_4 ), .out_2(\not16_修改引脚_2_out_2 ));
  Adder #(.width(16)) adder_1 (
    .a(\mux16_修改了引脚_3_out_4 ), .b(\mux16_修改了引脚_4_out_4 ), .out(adder_1_out));  // open: cin, cout
  \AND_修改了引脚  \and_修改了引脚_1  (.in_1(\mux16_修改了引脚_3_out_4 ), .in_2(\mux16_修改了引脚_4_out_4 ), .out_3(\and_修改了引脚_1_out_3 ));
  \Mux16_修改了引脚  \mux16_修改了引脚_5  (
    .in_2(\and_修改了引脚_1_out_3 ), .in_3(adder_1_out), .out_4(\mux16_修改了引脚_5_out_4 ), .in_1(in_3));
  \not16_修改引脚  \not16_修改引脚_3  (.in_1(\mux16_修改了引脚_5_out_4 ), .out_2(\not16_修改引脚_3_out_2 ));
  \Mux16_修改了引脚  \mux16_修改了引脚_6  (.in_2(\mux16_修改了引脚_5_out_4 ), .in_3(\not16_修改引脚_3_out_2 ), .out_4(out_9), .in_1(in_4));
  Or8Way or8way_1 (
    .in_1(out_9[0]), .in_2(out_9[1]), .in_3(out_9[2]), .in_4(out_9[3]), .in_5(out_9[4]), .in_6(out_9[5]),
    .in_7(out_9[6]), .in_8(out_9[7]), .out_9(or8way_1_out_9));
  Or8Way or8way_2 (
    .in_1(out_9[8]), .in_2(out_9[9]), .in_3(out_9[10]), .in_4(out_9[11]), .in_5(out_9[12]), .in_6(out_9[13]),
    .in_7(out_9[14]), .in_8(out_9[15]), .out_9(or8way_2_out_9));
  OR or_1 (.in_1(or8way_1_out_9), .in_2(or8way_2_out_9), .out_3(or_1_out_3));
  Not not_1 (.in_1(or_1_out_3), .out_2(out_11));

  assign out_10 = out_9[15];
endmodule

module \PC_修改了引脚  (
  input  in_1,
  input  in_2,
  input  in_3,
  input  [15:0] in_4,
  input  in_5,
  output [15:0] out_6
);

  wire [15:0] inc16_1_out_18, \mux16_修改了引脚_1_out_4 , \mux16_修改了引脚_2_out_4 , \mux16_修改了引脚_3_out_4 ;

  \Mux16_修改了引脚  \mux16_修改了引脚_1  (.in_2(out_6), .in_3(inc16_1_out_18), .out_4(\mux16_修改了引脚_1_out_4 ), .in_1(in_1));
  \Mux16_修改了引脚  \mux16_修改了引脚_2  (.in_2(\mux16_修改了引脚_1_out_4 ), .in_3(in_4), .out_4(\mux16_修改了引脚_2_out_4 ), .in_1(in_2));
  \Mux16_修改了引脚  \mux16_修改了引脚_3  (
    .in_2(\mux16_修改了引脚_2_out_4 ), .in_3({16{1'b0}}), .out_4(\mux16_修改了引脚_3_out_4 ), .in_1(in_3));
  Register_part #(.width(16)) register_1 (.D(\mux16_修改了引脚_3_out_4 ), .Q(out_6), .clk(in_5));  // open: en, clr
  Inc16 inc16_1 (
    .out_18(inc16_1_out_18[0]), .out_19(inc16_1_out_18[1]), .out_20(inc16_1_out_18[2]),
    .out_21(inc16_1_out_18[3]), .out_22(inc16_1_out_18[4]), .out_23(inc16_1_out_18[5]),
    .out_24(inc16_1_out_18[6]), .out_25(inc16_1_out_18[7]), .out_26(inc16_1_out_18[8]),
    .out_27(inc16_1_out_18[9]), .out_28(inc16_1_out_18[10]), .out_29(inc16_1_out_18[11]),
    .out_30(inc16_1_out_18[12]), .out_31(inc16_1_out_18[13]), .out_32(inc16_1_out_18[14]),
    .out_33(inc16_1_out_18[15]), .in_1(out_6[0]), .in_3(out_6[1]), .in_4(out_6[2]), .in_5(out_6[3]),
    .in_6(out_6[4]), .in_7(out_6[5]), .in_8(out_6[6]), .in_9(out_6[7]), .in_10(out_6[8]), .in_11(out_6[9]),
    .in_12(out_6[10]), .in_13(out_6[11]), .in_14(out_6[12]), .in_15(out_6[13]), .in_16(out_6[14]),
    .in_17(out_6[15]), .in_2(1'b1));

  // Notes on the sheet:
  //   inc
  //   load
  //   reset
endmodule

module CPU (
  input  [15:0] in_1,
  input  [15:0] in_2,
  input  reset,
  input  in_4,
  input  in_5,
  input  in_6,
  output out_7,
  output [15:0] adress_15,
  output [15:0] out_9,
  output [15:0] out_10
);

  wire \alu_采用了内置加法器_修改了引脚_1_out_10 , \alu_采用了内置加法器_修改了引脚_1_out_11 , and_2_out_3, and_3_out_3, and_4_out_3,
       not_1_out_2, not_2_out_2, or_1_out_3, or_2_out_3, or_3_out_3, or_4_out_3;
  wire [15:0] \mux16_修改了引脚_1_out_4 , \mux16_修改了引脚_2_out_4 , \mux16_修改了引脚_3_out_4 , register_2_q;

  Not not_1 (.in_1(in_1[15]), .out_2(not_1_out_2));
  \Mux16_修改了引脚  \mux16_修改了引脚_1  (.in_2({16{1'b0}}), .in_3(in_1), .out_4(\mux16_修改了引脚_1_out_4 ), .in_1(in_1[15]));
  \Mux16_修改了引脚  \mux16_修改了引脚_2  (.in_2(in_1), .in_3(out_9), .out_4(\mux16_修改了引脚_2_out_4 ), .in_1(in_1[15]));
  Register_part #(.width(16)) register_1 (
    .D(\mux16_修改了引脚_2_out_4 ), .en(or_1_out_3), .Q(adress_15), .clk(in_5));  // open: clr
  OR or_1 (.in_1(not_1_out_2), .in_2(in_1[5]), .out_3(or_1_out_3));
  AND and_1 (.in_1(in_1[3]), .in_2(in_1[15]), .out_3(out_7));
  \Mux16_修改了引脚  \mux16_修改了引脚_3  (.in_2(adress_15), .in_3(in_2), .out_4(\mux16_修改了引脚_3_out_4 ), .in_1(in_1[12]));
  \ALU_采用了内置加法器_修改了引脚  \alu_采用了内置加法器_修改了引脚_1  (
    .in_5(register_2_q), .out_9(out_9), .out_10(\alu_采用了内置加法器_修改了引脚_1_out_10 ),
    .out_11(\alu_采用了内置加法器_修改了引脚_1_out_11 ), .in_1(in_1[11]), .in_6(in_1[9]), .in_2(in_1[10]), .in_7(in_1[8]),
    .in_3(in_1[7]), .in_4(in_1[6]), .in_8(\mux16_修改了引脚_3_out_4 ));
  Register_part #(.width(16)) register_2 (
    .D(out_9), .en(\mux16_修改了引脚_1_out_4 [4]), .Q(register_2_q), .clk(in_6));  // open: clr
  AND and_2 (.in_1(\mux16_修改了引脚_1_out_4 [2]), .in_2(\alu_采用了内置加法器_修改了引脚_1_out_10 ), .out_3(and_2_out_3));
  AND and_3 (.in_1(\mux16_修改了引脚_1_out_4 [1]), .in_2(\alu_采用了内置加法器_修改了引脚_1_out_11 ), .out_3(and_3_out_3));
  OR or_2 (.in_1(\alu_采用了内置加法器_修改了引脚_1_out_10 ), .in_2(\alu_采用了内置加法器_修改了引脚_1_out_11 ), .out_3(or_2_out_3));
  Not not_2 (.in_1(or_2_out_3), .out_2(not_2_out_2));
  OR or_3 (.in_1(and_2_out_3), .in_2(and_3_out_3), .out_3(or_3_out_3));
  AND and_4 (.in_1(\mux16_修改了引脚_1_out_4 [0]), .in_2(not_2_out_2), .out_3(and_4_out_3));
  OR or_4 (.in_1(and_4_out_3), .in_2(or_3_out_3), .out_3(or_4_out_3));
  \PC_修改了引脚  \pc_修改了引脚_1  (
    .in_4(\mux16_修改了引脚_3_out_4 ), .out_6(out_10), .in_1(1'b1), .in_2(or_4_out_3), .in_3(reset), .in_5(in_4));

  // Notes on the sheet:
  //   instruction
  //   inM
  //   C
  //   outM
  //   15
  //   5
  //   Aregister
  //   3
  //   12
  //   9
  //   10
  //   11
  //   8
  //   7
  //   6
  //   Dregister
  //   WriteM
  //   PC[15]
endmodule

module Memory (
  input  in_1,
  input  in_2,
  input  in_3,
  input  in_4,
  input  in_5,
  input  in_6,
  input  in_7,
  input  in_8,
  input  in_9,
  input  in_10,
  input  in_11,
  input  in_12,
  input  in_13,
  input  in_14,
  input  in_15,
  input  _14,
  input  [15:0] in_17,
  input  [6:0] in_18,
  input  in_19,
  output [15:0] out_20
);

  wire dmux_1_out_3, dmux_1_out_4;
  wire [15:0] \mux16_修改了引脚_1_out_4 , ram8k_1_out_5, \ram16k_使用三态门_采用内置ram_1_out_5 ;
  wire [15:7] undriven;

  DMux dmux_1 (.in_1(in_1), .in_2(_14), .out_3(dmux_1_out_3), .out_4(dmux_1_out_4));
  \RAM16K_使用三态门_采用内置RAM  \ram16k_使用三态门_采用内置ram_1  (
    .in_1(in_17), .out_5(\ram16k_使用三态门_采用内置ram_1_out_5 ),
    .in_2({in_2, in_3, in_4, in_5, in_6, in_7, in_8, in_9, in_10, in_11, in_12, in_13, in_14, in_15}),
    .in_4(in_19), .in_3(dmux_1_out_3));
  RAM8k ram8k_1 (
    .in_1(in_17), .out_5(ram8k_1_out_5),
    .in_2({in_3, in_4, in_5, in_6, in_7, in_8, in_9, in_10, in_11, in_12, in_13, in_14, in_15}),
    .in_4(in_19), .in_3(dmux_1_out_4));
  \Mux16_修改了引脚  \mux16_修改了引脚_1  (
    .in_2(ram8k_1_out_5), .in_3({undriven, in_18}), .out_4(\mux16_修改了引脚_1_out_4 ), .in_1(in_2));
  \Mux16_修改了引脚  \mux16_修改了引脚_2  (
    .in_2(\ram16k_使用三态门_采用内置ram_1_out_5 ), .in_3(\mux16_修改了引脚_1_out_4 ), .out_4(out_20), .in_1(in_1));

  // Notes on the sheet:
  //   load
  //   in
  //   13
  //   14
endmodule

module computer (
  input  in_1
);

  wire clock_1_out, clock_2_out, clock_3_out, clock_4_out, cpu_1_out_7;
  wire [3:0] register_1_q, register_1_q_2, register_1_q_3, register_1_q_4;
  wire [15:0] cpu_1_adress_15, cpu_1_out_9, cpu_1_out_10, memory_1_out_20, rom_1_data;

  ROM #(.addrWidth(16), .dataWidth(16)) rom_1 (.addr(cpu_1_out_10), .data(rom_1_data));  // open: sel
  CPU cpu_1 (
    .in_1(rom_1_data), .in_2({register_1_q_4, register_1_q_3, register_1_q_2, register_1_q}), .reset(in_1),
    .out_9(cpu_1_out_9), .adress_15(cpu_1_adress_15), .out_7(cpu_1_out_7), .out_10(cpu_1_out_10),
    .in_4(clock_1_out), .in_5(clock_2_out), .in_6(clock_3_out));
  Clock #(.highDuration(4), .lowDuration(4)) clock_1 (.out(clock_1_out));
  Clock #(.highDuration(7)) clock_2 (.out(clock_2_out));
  Clock #(.highDuration(5), .lowDuration(3)) clock_3 (.out(clock_3_out));
  Memory memory_1 (
    ._14(cpu_1_out_7), .in_17(cpu_1_out_9), .in_15(cpu_1_adress_15[0]), .in_14(cpu_1_adress_15[1]),
    .in_13(cpu_1_adress_15[2]), .in_12(cpu_1_adress_15[3]), .in_11(cpu_1_adress_15[4]),
    .in_10(cpu_1_adress_15[5]), .in_9(cpu_1_adress_15[6]), .in_8(cpu_1_adress_15[7]),
    .in_7(cpu_1_adress_15[8]), .in_6(cpu_1_adress_15[9]), .in_5(cpu_1_adress_15[10]),
    .in_4(cpu_1_adress_15[11]), .in_3(cpu_1_adress_15[12]), .in_2(cpu_1_adress_15[13]),
    .in_1(cpu_1_adress_15[14]), .out_20(memory_1_out_20), .in_19(clock_4_out));  // open: in_18
  Register_part #(.width(16)) register_1 (
    .D(memory_1_out_20), .Q({register_1_q_4, register_1_q_3, register_1_q_2, register_1_q}), .clk(clock_4_out));  // open: en, clr
  Clock #(.highDuration(6), .lowDuration(2)) clock_4 (.out(clock_4_out));
  Hex_Digit_Display hex_digit_display_1 (.value(register_1_q_4));  // open: dp
  Hex_Digit_Display hex_digit_display_2 (.value(register_1_q_3));  // open: dp
  Hex_Digit_Display hex_digit_display_3 (.value(register_1_q_2));  // open: dp
  Hex_Digit_Display hex_digit_display_4 (.value(register_1_q));  // open: dp

  // Notes on the sheet:
  //   contents of rom_1 (hex, n*v repeats v):
  //   10 efc8 12 ea88 10 fc10 64 e4d0 12 e301 10 fc10 12 f088 10 fdc8 4 ea87 12 ea87
  //   13ba
endmodule

module \输出  (
  input  [15:0] in_1,
  output [6:0] out_2,
  output out_3
);

  wire clock_1_out;

  Clock clock_1 (.out(clock_1_out));
  Keyboard keyboard_1 (.clk(clock_1_out), .avail(out_3), .data(out_2));  // open: re, clr
  TTY tty_1 ();  // open: data, clk, we, clr
  DotMatrix #(.inputtype("row"), .matrixcols(16), .matrixrows(32), .dotshape("circle")) dotmatrix_1 (.row0(in_1));  // open: row1, row2, row3, row4, row5, row6, row7, row8, row9, row10, row11, row12, row13, row14, row15, row16, row17, row18, row19, row20, row21, row22, row23, row24, row25, row26, row27, row28, row29, row30, row31
endmodule
